// Logisim project xCPU-5.10.circ as structural Verilog: 30 circuits, main circuit main
// 4 KWord Memory
module main (
  input  in_1
);

  wire ac_1_ac_0, ac_1_ac_15, ac_1_add, ac_1_and, ac_1_com, ac_1_dr, ac_1_inpr, ac_1_ld, ac_1_shl, ac_1_shr,
       alu_1_cout, clock_1_out, control_unit_1_d0, control_unit_1_d1, control_unit_1_d2, control_unit_1_d3,
       control_unit_1_d4, control_unit_1_d5, control_unit_1_d6, control_unit_1_d7, control_unit_1_t0,
       control_unit_1_t1, control_unit_1_t2, control_unit_1_t3, control_unit_1_t4, control_unit_1_t5,
       control_unit_1_t6, fgi_1_fgi, fgo_1_fgo, flag_e_1_e, flag_i_1_i, flag_ien_1_ien, flag_r_1_r,
       ir_1_ir_15;
  wire [7:0] inpr_1_output;
  wire [15:0] ac_1_output, alu_1_output, dr_1_output, ir_1_output;

  FLAG_I flag_i_1 (.CLK(clock_1_out), .IR_15(ir_1_ir_15), .R(flag_r_1_r), .T2(control_unit_1_t2), .I(flag_i_1_i));
  FLAG_S flag_s_1 (.CLK(clock_1_out), .I(flag_i_1_i), .T3(control_unit_1_t3), .D7(control_unit_1_d7));  // open: B0, S
  FLAG_R flag_r_1 (
    .CLK(clock_1_out), .IEN(flag_ien_1_ien), .FGI(fgi_1_fgi), .FGO(fgo_1_fgo), .T0(control_unit_1_t0),
    .T1(control_unit_1_t1), .T2(control_unit_1_t2), .R(flag_r_1_r));
  FLAG_IEN flag_ien_1 (
    .CLK(clock_1_out), .I(flag_i_1_i), .R(flag_r_1_r), .T2(control_unit_1_t2), .T3(control_unit_1_t3),
    .D7(control_unit_1_d7), .IEN(flag_ien_1_ien));  // open: B6, B7
  FGI fgi_1 (
    .CLK(clock_1_out), .I(flag_i_1_i), .T3(control_unit_1_t3), .D7(control_unit_1_d7), .FGI(fgi_1_fgi));  // open: B11
  FGO fgo_1 (
    .CLK(clock_1_out), .I(flag_i_1_i), .T3(control_unit_1_t3), .D7(control_unit_1_d7), .FGO(fgo_1_fgo));  // open: B10
  FLAG_E flag_e_1 (
    .CLK(clock_1_out), .Cout(alu_1_cout), .AC_15(ac_1_ac_15), .AC_0(ac_1_ac_0), .I(flag_i_1_i),
    .T3(control_unit_1_t3), .T5(control_unit_1_t5), .D1(control_unit_1_d1), .D7(control_unit_1_d7),
    .E(flag_e_1_e));  // open: B6, B7, B8, B10
  Control_Unit control_unit_1 (
    .CLK(clock_1_out), .FLAG_I(flag_i_1_i), .FLAG_R(flag_r_1_r), .IR_IN(ir_1_output), .SC_INC(in_1),
    .D0(control_unit_1_d0), .D1(control_unit_1_d1), .D2(control_unit_1_d2), .D3(control_unit_1_d3),
    .D4(control_unit_1_d4), .D5(control_unit_1_d5), .D6(control_unit_1_d6), .D7(control_unit_1_d7),
    .I(flag_i_1_i), .T0(control_unit_1_t0), .T1(control_unit_1_t1), .T2(control_unit_1_t2),
    .T3(control_unit_1_t3), .T4(control_unit_1_t4), .T5(control_unit_1_t5), .T6(control_unit_1_t6));  // open: T7, T8, T9, T10, T11, T12, T13, T14, T15
  Clock clock_1 (.out(clock_1_out));
  ALU alu_1 (
    .CLK(clock_1_out), .LD(ac_1_ld), .AND(ac_1_and), .ADD(ac_1_add), .DR(ac_1_dr), .INPR(ac_1_inpr),
    .COM(ac_1_com), .SHR(ac_1_shr), .SHL(ac_1_shl), .AC_INPUT(ac_1_output), .DR_INPUT(dr_1_output),
    .INPR_INPUT(inpr_1_output), .OUTPUT(alu_1_output), .Cout(alu_1_cout));
  Memory memory_1 (
    .CLK(clock_1_out), .I(flag_i_1_i), .R(flag_r_1_r), .T1(control_unit_1_t1), .T3(control_unit_1_t3),
    .T4(control_unit_1_t4), .T6(control_unit_1_t6), .D0(control_unit_1_d0), .D1(control_unit_1_d1),
    .D2(control_unit_1_d2), .D3(control_unit_1_d3), .D5(control_unit_1_d5), .D6(control_unit_1_d6),
    .D7(control_unit_1_d7));  // open: Address, DATA_IN, DATA_OUT
  AR ar_1 (
    .CLK(clock_1_out), .I(flag_i_1_i), .R(flag_r_1_r), .T0(control_unit_1_t0), .T2(control_unit_1_t2),
    .T3(control_unit_1_t3), .T4(control_unit_1_t4), .D7(control_unit_1_d7), .D5(control_unit_1_d5));  // open: INPUT, OUTPUT
  PC pc_1 (
    .CLK(clock_1_out), .AC_15(ac_1_ac_15), .AC_0(ac_1_ac_0), .I(flag_i_1_i), .E(flag_e_1_e), .R(flag_r_1_r),
    .IEN(flag_ien_1_ien), .FGI(fgi_1_fgi), .FGO(fgo_1_fgo), .T1(control_unit_1_t1), .T3(control_unit_1_t3),
    .T4(control_unit_1_t4), .T5(control_unit_1_t5), .D4(control_unit_1_d4), .D5(control_unit_1_d5),
    .D7(control_unit_1_d7));  // open: B1, B2, B3, B4, B8, B9, input, output
  DR dr_1 (
    .CLK(clock_1_out), .T4(control_unit_1_t4), .T5(control_unit_1_t5), .T6(control_unit_1_t6),
    .D0(control_unit_1_d0), .D1(control_unit_1_d1), .D2(control_unit_1_d2), .D6(control_unit_1_d6),
    .\output (dr_1_output));  // open: Input
  TR tr_1 (
    .CLK(clock_1_out), .R(flag_r_1_r), .IEN(flag_ien_1_ien), .FGI(fgi_1_fgi), .FGO(fgo_1_fgo),
    .T0(control_unit_1_t0));  // open: input, output
  AC ac_1 (
    .CLK(clock_1_out), .I(flag_i_1_i), .E(flag_e_1_e), .T3(control_unit_1_t3), .T4(control_unit_1_t4),
    .T5(control_unit_1_t5), .D0(control_unit_1_d0), .D1(control_unit_1_d1), .D2(control_unit_1_d2),
    .D7(control_unit_1_d7), .INPUT(alu_1_output), .AC_0(ac_1_ac_0), .AC_15(ac_1_ac_15), .OUTPUT(ac_1_output),
    .LD(ac_1_ld), .AND(ac_1_and), .ADD(ac_1_add), .DR(ac_1_dr), .INPR(ac_1_inpr), .COM(ac_1_com),
    .SHR(ac_1_shr), .SHL(ac_1_shl));  // open: B5, B6, B7, B9, B11
  IR ir_1 (
    .CLK(clock_1_out), .R(flag_r_1_r), .T1(control_unit_1_t1), .IR_15(ir_1_ir_15), .\output (ir_1_output));  // open: input
  OUTR outr_1 (
    .CLK(clock_1_out), .I(flag_i_1_i), .T3(control_unit_1_t3), .D7(control_unit_1_d7));  // open: B10, input, output
  LED led_1 (.in(control_unit_1_t1));
  LED led_2 (.in(control_unit_1_t3));
  LED led_3 (.in(control_unit_1_t4));
  INPR inpr_1 (.CLK(clock_1_out), .\output (inpr_1_output));  // open: input
  BUS_SELEC bus_selec_1 ();  // open: I, R, T0, T1, T2, T3, T4, T5, T6, D0, D1, D2, D3, D4, D5, D6, D7, out_18
  L_8_Bit_Bus l_8_bit_bus_1 ();  // open: SELECT, AR_1, DR_2, AC_3, IR_4, TR_5, TR_6, IR_7, Output_0, Output_1, Output_2, Output_3, Output_4, Output_5, Output_6, Output_7

  // Notes on the sheet:
  //   control unit içerisindeki IR'yi kontrol et
endmodule

// 1 Bit A Reg
module L_1_Bit_A_Register (
  input  Input_1,
  input  Input_2,
  input  Input_3,
  input  Input_4,
  input  Input_5,
  input  CLK,
  output Output_1
);

  wire or_1_out, or_2_out;

  or or_1 (or_1_out, Input_1, Input_2);
  or or_2 (or_2_out, Input_3, Input_4, Input_5);
  J_K_Flip_Flop j_k_ff_1 (.J(or_1_out), .clk(CLK), .K(or_2_out), .Q(Output_1));  // open: Qn, preset, en, reset

  // Notes on the sheet:
  //   J1
  //   J2
  //   K1
  //   K2
  //   K3
  //   OUTPUT
endmodule

// 12 Bit A REG (INC,LD,CLR)
module L_12_Bit_A_Register (
  input  CLR,
  input  LD,
  input  INC,
  input  INPUT_0,
  input  INPUT_1,
  input  INPUT_2,
  input  INPUT_3,
  input  INPUT_4,
  input  INPUT_5,
  input  INPUT_6,
  input  INPUT_7,
  input  INPUT_8,
  input  INPUT_9,
  input  INPUT_10,
  input  INPUT_11,
  input  CLK,
  output OUTPUT_0,
  output OUTPUT_1,
  output OUTPUT_2,
  output OUTPUT_3,
  output OUTPUT_4,
  output OUTPUT_5,
  output OUTPUT_6,
  output OUTPUT_7,
  output OUTPUT_8,
  output OUTPUT_9,
  output OUTPUT_10,
  output OUTPUT_11,
  output Cout
);

  wire and_1_out, and_2_out, and_3_out, and_4_out, and_5_out, and_6_out, and_7_out, and_8_out, and_9_out,
       and_10_out, and_11_out, and_12_out, and_13_out, and_14_out, and_15_out, and_16_out, and_17_out,
       and_18_out, and_19_out, and_20_out, and_21_out, and_22_out, and_23_out, and_24_out, and_25_out,
       and_26_out, and_27_out, and_28_out, and_29_out, and_30_out, and_31_out, and_32_out, and_33_out,
       and_34_out, and_35_out, and_36_out, and_37_out;

  and and_1 (and_1_out, ~CLR, LD);  // AND_Gate
  and and_2 (and_2_out, and_1_out, INPUT_0);
  and and_3 (and_3_out, and_1_out, ~INPUT_0);  // AND_Gate
  and and_4 (and_4_out, and_1_out, INPUT_1);
  and and_5 (and_5_out, and_1_out, ~INPUT_1);  // AND_Gate
  and and_6 (and_6_out, and_1_out, INPUT_2);
  and and_7 (and_7_out, and_1_out, ~INPUT_2);  // AND_Gate
  and and_8 (and_8_out, and_1_out, INPUT_3);
  and and_9 (and_9_out, and_1_out, ~INPUT_3);  // AND_Gate
  and and_10 (and_10_out, and_1_out, INPUT_4);
  and and_11 (and_11_out, and_1_out, ~INPUT_4);  // AND_Gate
  and and_12 (and_12_out, and_1_out, INPUT_5);
  and and_13 (and_13_out, and_1_out, ~INPUT_5);  // AND_Gate
  and and_14 (and_14_out, and_1_out, INPUT_6);
  and and_15 (and_15_out, and_1_out, ~INPUT_6);  // AND_Gate
  and and_16 (and_16_out, and_1_out, INPUT_7);
  and and_17 (and_17_out, and_1_out, ~INPUT_7);  // AND_Gate
  and and_18 (and_18_out, and_1_out, INPUT_8);
  and and_19 (and_19_out, and_1_out, ~INPUT_8);  // AND_Gate
  and and_20 (and_20_out, and_1_out, INPUT_9);
  and and_21 (and_21_out, and_1_out, ~INPUT_9);  // AND_Gate
  and and_22 (and_22_out, and_1_out, INPUT_10);
  and and_23 (and_23_out, and_1_out, ~INPUT_10);  // AND_Gate
  and and_24 (and_24_out, and_1_out, INPUT_11);
  and and_25 (and_25_out, and_1_out, ~INPUT_11);  // AND_Gate
  and and_26 (and_26_out, ~CLR, ~LD, INC);  // AND_Gate
  L_1_Bit_A_Register _1 (
    .Input_1(and_26_out), .Input_2(and_2_out), .Input_3(CLR), .Input_4(and_26_out), .Input_5(and_3_out),
    .CLK(CLK), .Output_1(OUTPUT_0));
  and and_27 (and_27_out, OUTPUT_0, and_26_out);
  L_1_Bit_A_Register l_1_bit_a_register_1 (
    .Input_1(and_27_out), .Input_2(and_4_out), .Input_3(CLR), .Input_4(and_27_out), .Input_5(and_5_out),
    .CLK(CLK), .Output_1(OUTPUT_1));
  and and_28 (and_28_out, OUTPUT_1, and_27_out);
  L_1_Bit_A_Register l_1_bit_a_register_2 (
    .Input_1(and_28_out), .Input_2(and_6_out), .Input_3(CLR), .Input_4(and_28_out), .Input_5(and_7_out),
    .CLK(CLK), .Output_1(OUTPUT_2));
  and and_29 (and_29_out, and_28_out, and_28_out);
  L_1_Bit_A_Register l_1_bit_a_register_3 (
    .Input_1(and_29_out), .Input_2(and_8_out), .Input_3(CLR), .Input_4(and_29_out), .Input_5(and_9_out),
    .CLK(CLK), .Output_1(OUTPUT_3));
  and and_30 (and_30_out, OUTPUT_3, and_29_out);
  L_1_Bit_A_Register l_1_bit_a_register_4 (
    .Input_1(and_30_out), .Input_2(and_10_out), .Input_3(CLR), .Input_4(and_30_out), .Input_5(and_11_out),
    .CLK(CLK), .Output_1(OUTPUT_4));
  and and_31 (and_31_out, OUTPUT_4, and_30_out);
  L_1_Bit_A_Register l_1_bit_a_register_5 (
    .Input_1(and_31_out), .Input_2(and_12_out), .Input_3(CLR), .Input_4(and_31_out), .Input_5(and_13_out),
    .CLK(CLK), .Output_1(OUTPUT_5));
  and and_32 (and_32_out, OUTPUT_5, and_31_out);
  L_1_Bit_A_Register l_1_bit_a_register_6 (
    .Input_1(and_32_out), .Input_2(and_14_out), .Input_3(CLR), .Input_4(and_32_out), .Input_5(and_15_out),
    .CLK(CLK), .Output_1(OUTPUT_6));
  and and_33 (and_33_out, OUTPUT_6, and_32_out);
  L_1_Bit_A_Register l_1_bit_a_register_7 (
    .Input_1(and_33_out), .Input_2(and_16_out), .Input_3(CLR), .Input_4(and_33_out), .Input_5(and_17_out),
    .CLK(CLK), .Output_1(OUTPUT_7));
  and and_34 (and_34_out, OUTPUT_7, and_33_out);
  L_1_Bit_A_Register l_1_bit_a_register_8 (
    .Input_1(and_34_out), .Input_2(and_18_out), .Input_3(CLR), .Input_4(and_34_out), .Input_5(and_19_out),
    .CLK(CLK), .Output_1(OUTPUT_8));
  and and_35 (and_35_out, OUTPUT_8, and_34_out);
  L_1_Bit_A_Register l_1_bit_a_register_9 (
    .Input_1(and_35_out), .Input_2(and_20_out), .Input_3(CLR), .Input_4(and_35_out), .Input_5(and_21_out),
    .CLK(CLK), .Output_1(OUTPUT_9));
  and and_36 (and_36_out, OUTPUT_9, and_35_out);
  L_1_Bit_A_Register l_1_bit_a_register_10 (
    .Input_1(and_36_out), .Input_2(and_22_out), .Input_3(CLR), .Input_4(and_36_out), .Input_5(and_23_out),
    .CLK(CLK), .Output_1(OUTPUT_10));
  and and_37 (and_37_out, OUTPUT_10, and_36_out);
  L_1_Bit_A_Register l_1_bit_a_register_11 (
    .Input_1(and_37_out), .Input_2(and_24_out), .Input_3(CLR), .Input_4(and_37_out), .Input_5(and_25_out),
    .CLK(CLK), .Output_1(OUTPUT_11));
  and and_38 (Cout, OUTPUT_11, and_37_out);
endmodule

// 16 Bit A REG (INC,LD,CLR)
module L_16_Bit_A_Register (
  input  CLR,
  input  LD,
  input  INC,
  input  INPUT_0,
  input  INPUT_1,
  input  INPUT_2,
  input  INPUT_3,
  input  INPUT_4,
  input  INPUT_5,
  input  INPUT_6,
  input  INPUT_7,
  input  INPUT_8,
  input  INPUT_9,
  input  INPUT_10,
  input  INPUT_11,
  input  INPUT_12,
  input  INPUT_13,
  input  INPUT_14,
  input  INPUT_15,
  input  CLK,
  output OUTPUT_0,
  output OUTPUT_1,
  output OUTPUT_2,
  output OUTPUT_3,
  output OUTPUT_4,
  output OUTPUT_5,
  output OUTPUT_6,
  output OUTPUT_7,
  output OUTPUT_8,
  output OUTPUT_9,
  output OUTPUT_10,
  output OUTPUT_11,
  output OUTPUT_12,
  output OUTPUT_13,
  output OUTPUT_14,
  output OUTPUT_15,
  output Eout
);

  wire and_1_out, and_2_out, and_3_out, and_4_out, and_5_out, and_6_out, and_7_out, and_8_out, and_9_out,
       and_10_out, and_11_out, and_12_out, and_13_out, and_14_out, and_15_out, and_16_out, and_17_out,
       and_18_out, and_19_out, and_20_out, and_21_out, and_22_out, and_23_out, and_24_out, and_25_out,
       and_26_out, and_27_out, and_28_out, and_29_out, and_30_out, and_31_out, and_32_out, and_33_out,
       and_34_out, and_35_out, and_36_out, and_37_out, and_38_out, and_39_out, and_40_out, and_41_out,
       and_42_out, and_43_out, and_44_out, and_45_out, and_46_out, and_47_out, and_48_out, and_49_out;

  and and_1 (and_1_out, ~CLR, LD);  // AND_Gate
  and and_2 (and_2_out, ~CLR, ~LD, INC);  // AND_Gate
  and and_3 (and_3_out, and_1_out, INPUT_0);
  and and_4 (and_4_out, and_1_out, ~INPUT_0);  // AND_Gate
  and and_5 (and_5_out, and_1_out, INPUT_1);
  and and_6 (and_6_out, and_1_out, ~INPUT_1);  // AND_Gate
  and and_7 (and_7_out, and_1_out, INPUT_2);
  and and_8 (and_8_out, and_1_out, ~INPUT_2);  // AND_Gate
  and and_9 (and_9_out, and_1_out, INPUT_3);
  and and_10 (and_10_out, and_1_out, ~INPUT_3);  // AND_Gate
  and and_11 (and_11_out, and_1_out, INPUT_4);
  and and_12 (and_12_out, and_1_out, ~INPUT_4);  // AND_Gate
  and and_13 (and_13_out, and_1_out, INPUT_5);
  and and_14 (and_14_out, and_1_out, ~INPUT_5);  // AND_Gate
  and and_15 (and_15_out, and_1_out, INPUT_6);
  and and_16 (and_16_out, and_1_out, ~INPUT_6);  // AND_Gate
  and and_17 (and_17_out, and_1_out, INPUT_7);
  and and_18 (and_18_out, and_1_out, ~INPUT_7);  // AND_Gate
  and and_19 (and_19_out, and_1_out, INPUT_8);
  and and_20 (and_20_out, and_1_out, ~INPUT_8);  // AND_Gate
  and and_21 (and_21_out, and_1_out, INPUT_9);
  and and_22 (and_22_out, and_1_out, ~INPUT_9);  // AND_Gate
  and and_23 (and_23_out, and_1_out, INPUT_10);
  and and_24 (and_24_out, and_1_out, ~INPUT_10);  // AND_Gate
  and and_25 (and_25_out, and_1_out, INPUT_11);
  and and_26 (and_26_out, and_1_out, ~INPUT_11);  // AND_Gate
  and and_27 (and_27_out, and_1_out, INPUT_12);
  and and_28 (and_28_out, and_1_out, ~INPUT_12);  // AND_Gate
  and and_29 (and_29_out, and_1_out, INPUT_13);
  and and_30 (and_30_out, and_1_out, ~INPUT_13);  // AND_Gate
  and and_31 (and_31_out, and_1_out, INPUT_14);
  and and_32 (and_32_out, and_1_out, ~INPUT_14);  // AND_Gate
  and and_33 (and_33_out, and_1_out, INPUT_15);
  and and_34 (and_34_out, and_1_out, ~INPUT_15);  // AND_Gate
  L_1_Bit_A_Register l_1_bit_a_register_1 (
    .Input_1(and_2_out), .Input_2(and_3_out), .Input_3(CLR), .Input_4(and_2_out), .Input_5(and_4_out),
    .CLK(CLK), .Output_1(OUTPUT_0));
  and and_35 (and_35_out, OUTPUT_0, and_2_out);
  L_1_Bit_A_Register l_1_bit_a_register_2 (
    .Input_1(and_35_out), .Input_2(and_5_out), .Input_3(CLR), .Input_4(and_35_out), .Input_5(and_6_out),
    .CLK(CLK), .Output_1(OUTPUT_1));
  and and_36 (and_36_out, OUTPUT_1, and_35_out);
  L_1_Bit_A_Register l_1_bit_a_register_3 (
    .Input_1(and_36_out), .Input_2(and_7_out), .Input_3(CLR), .Input_4(and_36_out), .Input_5(and_8_out),
    .CLK(CLK), .Output_1(OUTPUT_2));
  and and_37 (and_37_out, OUTPUT_2, and_36_out);
  L_1_Bit_A_Register l_1_bit_a_register_4 (
    .Input_1(and_37_out), .Input_2(and_9_out), .Input_3(CLR), .Input_4(and_37_out), .Input_5(and_10_out),
    .CLK(CLK), .Output_1(OUTPUT_3));
  and and_38 (and_38_out, OUTPUT_3, and_37_out);
  L_1_Bit_A_Register l_1_bit_a_register_5 (
    .Input_1(and_38_out), .Input_2(and_11_out), .Input_3(CLR), .Input_4(and_38_out), .Input_5(and_12_out),
    .CLK(CLK), .Output_1(OUTPUT_4));
  and and_39 (and_39_out, OUTPUT_4, and_38_out);
  L_1_Bit_A_Register l_1_bit_a_register_6 (
    .Input_1(and_39_out), .Input_2(and_13_out), .Input_3(CLR), .Input_4(and_39_out), .Input_5(and_14_out),
    .CLK(CLK), .Output_1(OUTPUT_5));
  and and_40 (and_40_out, OUTPUT_5, and_39_out);
  L_1_Bit_A_Register l_1_bit_a_register_7 (
    .Input_1(and_40_out), .Input_2(and_15_out), .Input_3(CLR), .Input_4(and_40_out), .Input_5(and_16_out),
    .CLK(CLK), .Output_1(OUTPUT_6));
  and and_41 (and_41_out, OUTPUT_6, and_40_out);
  L_1_Bit_A_Register l_1_bit_a_register_8 (
    .Input_1(and_41_out), .Input_2(and_17_out), .Input_3(CLR), .Input_4(and_41_out), .Input_5(and_18_out),
    .CLK(CLK), .Output_1(OUTPUT_7));
  and and_42 (and_42_out, OUTPUT_7, and_41_out);
  L_1_Bit_A_Register l_1_bit_a_register_9 (
    .Input_1(and_42_out), .Input_2(and_19_out), .Input_3(CLR), .Input_4(and_42_out), .Input_5(and_20_out),
    .CLK(CLK), .Output_1(OUTPUT_8));
  and and_43 (and_43_out, OUTPUT_8, and_42_out);
  L_1_Bit_A_Register l_1_bit_a_register_10 (
    .Input_1(and_43_out), .Input_2(and_21_out), .Input_3(CLR), .Input_4(and_43_out), .Input_5(and_22_out),
    .CLK(CLK), .Output_1(OUTPUT_9));
  and and_44 (and_44_out, OUTPUT_9, and_43_out);
  L_1_Bit_A_Register l_1_bit_a_register_11 (
    .Input_1(and_44_out), .Input_2(and_23_out), .Input_3(CLR), .Input_4(and_44_out), .Input_5(and_24_out),
    .CLK(CLK), .Output_1(OUTPUT_10));
  and and_45 (and_45_out, OUTPUT_10, and_44_out);
  L_1_Bit_A_Register l_1_bit_a_register_12 (
    .Input_1(and_45_out), .Input_2(and_25_out), .Input_3(CLR), .Input_4(and_45_out), .Input_5(and_26_out),
    .CLK(CLK), .Output_1(OUTPUT_11));
  and and_46 (and_46_out, OUTPUT_11, and_45_out);
  L_1_Bit_A_Register l_1_bit_a_register_13 (
    .Input_1(and_46_out), .Input_2(and_27_out), .Input_3(CLR), .Input_4(and_46_out), .Input_5(and_28_out),
    .CLK(CLK), .Output_1(OUTPUT_12));
  and and_47 (and_47_out, OUTPUT_12, and_46_out);
  L_1_Bit_A_Register l_1_bit_a_register_14 (
    .Input_1(and_47_out), .Input_2(and_29_out), .Input_3(CLR), .Input_4(and_47_out), .Input_5(and_30_out),
    .CLK(CLK), .Output_1(OUTPUT_13));
  and and_48 (and_48_out, OUTPUT_13, and_47_out);
  L_1_Bit_A_Register l_1_bit_a_register_15 (
    .Input_1(and_48_out), .Input_2(and_31_out), .Input_3(CLR), .Input_4(and_48_out), .Input_5(and_32_out),
    .CLK(CLK), .Output_1(OUTPUT_14));
  and and_49 (and_49_out, OUTPUT_14, and_48_out);
  L_1_Bit_A_Register l_1_bit_a_register_16 (
    .Input_1(and_49_out), .Input_2(and_33_out), .Input_3(CLR), .Input_4(and_49_out), .Input_5(and_34_out),
    .CLK(CLK), .Output_1(OUTPUT_15));
  and and_50 (Eout, OUTPUT_15, and_49_out);
endmodule

// 1_Bit_B_Reg
module L_1_Bit_B_Reg (
  input  J1,
  input  J2,
  input  K1,
  input  K2,
  input  K3,
  input  CLK,
  output OUTPUT
);

  wire or_1_out, or_2_out;

  or or_1 (or_1_out, J1, J2);
  or or_2 (or_2_out, K1, K2, K3);
  J_K_Flip_Flop j_k_ff_1 (.J(or_1_out), .clk(CLK), .K(or_2_out), .Q(OUTPUT));  // open: Qn, preset, en, reset
endmodule

// 8 Bit B REG
module L_8_Bit_B_Reg (
  input  CLR,
  input  LD,
  input  INC,
  input  INPUT_0,
  input  INPUT_1,
  input  INPUT_2,
  input  INPUT_3,
  input  INPUT_4,
  input  INPUT_5,
  input  INPUT_6,
  input  INPUT_7,
  input  CLK,
  output OUTPUT_0,
  output OUTPUT_1,
  output OUTPUT_2,
  output OUTPUT_3,
  output OUTPUT_4,
  output OUTPUT_5,
  output OUTPUT_6,
  output OUTPUT_7
);

  wire and_1_out, and_2_out, and_3_out, and_4_out, and_5_out, and_6_out, and_7_out, and_8_out, and_9_out,
       and_10_out, and_11_out, and_12_out, and_13_out, and_14_out, and_15_out, and_16_out, and_17_out,
       and_18_out, and_19_out, and_20_out, and_21_out, and_22_out, and_23_out, and_24_out, and_25_out;

  and and_1 (and_1_out, ~CLR, LD);  // AND_Gate
  and and_2 (and_2_out, ~CLR, ~LD, INC);  // AND_Gate
  and and_3 (and_3_out, and_1_out, INPUT_0);
  and and_4 (and_4_out, and_1_out, ~INPUT_0);  // AND_Gate
  and and_5 (and_5_out, and_1_out, INPUT_1);
  and and_6 (and_6_out, and_1_out, ~INPUT_1);  // AND_Gate
  and and_7 (and_7_out, and_1_out, INPUT_2);
  and and_8 (and_8_out, and_1_out, ~INPUT_2);  // AND_Gate
  and and_9 (and_9_out, and_1_out, INPUT_3);
  and and_10 (and_10_out, and_1_out, ~INPUT_3);  // AND_Gate
  and and_11 (and_11_out, and_1_out, INPUT_4);
  and and_12 (and_12_out, and_1_out, ~INPUT_4);  // AND_Gate
  and and_13 (and_13_out, and_1_out, INPUT_5);
  and and_14 (and_14_out, and_1_out, ~INPUT_5);  // AND_Gate
  and and_15 (and_15_out, and_1_out, INPUT_6);
  and and_16 (and_16_out, and_1_out, ~INPUT_6);  // AND_Gate
  and and_17 (and_17_out, and_1_out, INPUT_7);
  and and_18 (and_18_out, and_1_out, ~INPUT_7);  // AND_Gate
  L_1_Bit_B_Reg l_1_bit_b_reg_1 (
    .J1(and_2_out), .J2(and_3_out), .K1(and_1_out), .K2(and_2_out), .K3(and_4_out), .CLK(CLK),
    .OUTPUT(OUTPUT_0));
  and and_19 (and_19_out, OUTPUT_0, and_2_out);
  L_1_Bit_B_Reg l_1_bit_b_reg_2 (
    .J1(and_19_out), .J2(and_5_out), .K1(and_1_out), .K2(and_19_out), .K3(and_6_out), .CLK(CLK),
    .OUTPUT(OUTPUT_1));
  and and_20 (and_20_out, OUTPUT_1, and_19_out);
  L_1_Bit_B_Reg l_1_bit_b_reg_3 (
    .J1(and_20_out), .J2(and_7_out), .K1(and_1_out), .K2(and_20_out), .K3(and_8_out), .CLK(CLK),
    .OUTPUT(OUTPUT_2));
  and and_21 (and_21_out, OUTPUT_2, and_20_out);
  L_1_Bit_B_Reg l_1_bit_b_reg_4 (
    .J1(and_21_out), .J2(and_9_out), .K1(and_1_out), .K2(and_21_out), .K3(and_10_out), .CLK(CLK),
    .OUTPUT(OUTPUT_3));
  and and_22 (and_22_out, OUTPUT_3, and_21_out);
  L_1_Bit_B_Reg l_1_bit_b_reg_5 (
    .J1(and_22_out), .J2(and_11_out), .K1(and_1_out), .K2(and_22_out), .K3(and_12_out), .CLK(CLK),
    .OUTPUT(OUTPUT_4));
  and and_23 (and_23_out, OUTPUT_4, and_22_out);
  L_1_Bit_B_Reg l_1_bit_b_reg_6 (
    .J1(and_23_out), .J2(and_13_out), .K1(and_1_out), .K2(and_23_out), .K3(and_14_out), .CLK(CLK),
    .OUTPUT(OUTPUT_5));
  and and_24 (and_24_out, OUTPUT_5, and_23_out);
  L_1_Bit_B_Reg l_1_bit_b_reg_7 (
    .J1(and_24_out), .J2(and_15_out), .K1(and_1_out), .K2(and_24_out), .K3(and_16_out), .CLK(CLK),
    .OUTPUT(OUTPUT_6));
  and and_25 (and_25_out, OUTPUT_6, and_24_out);
  L_1_Bit_B_Reg l_1_bit_b_reg_8 (
    .J1(and_25_out), .J2(and_17_out), .K1(and_1_out), .K2(and_25_out), .K3(and_18_out), .CLK(CLK),
    .OUTPUT(OUTPUT_7));
endmodule

// 16 Bit REG
module L_16_Bit_B_Reg (
  input  CLR,
  input  LD,
  input  INC,
  input  INPUT_0,
  input  INPUT_1,
  input  INPUT_2,
  input  INPUT_3,
  input  INPUT_4,
  input  INPUT_5,
  input  INPUT_6,
  input  INPUT_7,
  input  INPUT_8,
  input  INPUT_9,
  input  INPUT_10,
  input  INPUT_11,
  input  INPUT_12,
  input  INPUT_13,
  input  INPUT_14,
  input  INPUT_15,
  input  CLK,
  output OUTPUT_0,
  output OUTPUT_1,
  output OUTPUT_2,
  output OUTPUT_3,
  output OUTPUT_4,
  output OUTPUT_5,
  output OUTPUT_6,
  output OUTPUT_7,
  output OUTPUT_8,
  output OUTPUT_9,
  output OUTPUT_10,
  output OUTPUT_11,
  output OUTPUT_12,
  output OUTPUT_13,
  output OUTPUT_14,
  output OUTPUT_15
);

  wire and_1_out, and_2_out, and_3_out, and_4_out, and_5_out, and_6_out, and_7_out, and_8_out, and_9_out,
       and_10_out, and_11_out, and_12_out, and_13_out, and_14_out, and_15_out, and_16_out, and_17_out,
       and_18_out, and_19_out, and_20_out, and_21_out, and_22_out, and_23_out, and_24_out, and_25_out,
       and_26_out, and_27_out, and_28_out, and_29_out, and_30_out, and_31_out, and_32_out, and_33_out,
       and_34_out, and_35_out, and_36_out, and_37_out, and_38_out, and_39_out, and_40_out, and_41_out,
       and_42_out, and_43_out, and_44_out, and_45_out, and_46_out, and_47_out, and_48_out, and_49_out;

  and and_1 (and_1_out, ~CLR, LD);  // AND_Gate
  and and_2 (and_2_out, ~CLR, ~LD, INC);  // AND_Gate
  and and_3 (and_3_out, and_1_out, INPUT_0);
  and and_4 (and_4_out, and_1_out, ~INPUT_0);  // AND_Gate
  and and_5 (and_5_out, and_1_out, INPUT_1);
  and and_6 (and_6_out, and_1_out, ~INPUT_1);  // AND_Gate
  and and_7 (and_7_out, and_1_out, INPUT_2);
  and and_8 (and_8_out, and_1_out, ~INPUT_2);  // AND_Gate
  and and_9 (and_9_out, and_1_out, INPUT_3);
  and and_10 (and_10_out, and_1_out, ~INPUT_3);  // AND_Gate
  and and_11 (and_11_out, and_1_out, INPUT_4);
  and and_12 (and_12_out, and_1_out, ~INPUT_4);  // AND_Gate
  and and_13 (and_13_out, and_1_out, INPUT_5);
  and and_14 (and_14_out, and_1_out, ~INPUT_5);  // AND_Gate
  and and_15 (and_15_out, and_1_out, INPUT_6);
  and and_16 (and_16_out, and_1_out, ~INPUT_6);  // AND_Gate
  and and_17 (and_17_out, and_1_out, INPUT_7);
  and and_18 (and_18_out, and_1_out, ~INPUT_7);  // AND_Gate
  and and_19 (and_19_out, and_1_out, INPUT_8);
  and and_20 (and_20_out, and_1_out, ~INPUT_8);  // AND_Gate
  and and_21 (and_21_out, and_1_out, INPUT_9);
  and and_22 (and_22_out, and_1_out, ~INPUT_9);  // AND_Gate
  buf and_23 (and_23_out, INPUT_10);  // AND_Gate
  and and_24 (and_24_out, and_1_out, ~INPUT_10);  // AND_Gate
  and and_25 (and_25_out, and_1_out, INPUT_11);
  and and_26 (and_26_out, and_1_out, ~INPUT_11);  // AND_Gate
  and and_27 (and_27_out, and_1_out, INPUT_12);
  and and_28 (and_28_out, and_1_out, ~INPUT_12);  // AND_Gate
  and and_29 (and_29_out, and_1_out, INPUT_13);
  and and_30 (and_30_out, and_1_out, ~INPUT_13);  // AND_Gate
  and and_31 (and_31_out, and_1_out, INPUT_14);
  and and_32 (and_32_out, and_1_out, ~INPUT_14);  // AND_Gate
  and and_33 (and_33_out, and_1_out, INPUT_15);
  and and_34 (and_34_out, and_1_out, ~INPUT_15);  // AND_Gate
  and and_35 (and_35_out, OUTPUT_0, and_2_out);
  and and_36 (and_36_out, OUTPUT_1, and_35_out);
  and and_37 (and_37_out, OUTPUT_2, and_36_out);
  and and_38 (and_38_out, OUTPUT_3, and_37_out);
  and and_39 (and_39_out, OUTPUT_4, and_38_out);
  and and_40 (and_40_out, OUTPUT_5, and_39_out);
  and and_41 (and_41_out, OUTPUT_6, and_40_out);
  and and_42 (and_42_out, OUTPUT_7, and_41_out);
  and and_43 (and_43_out, OUTPUT_8, and_42_out);
  and and_44 (and_44_out, OUTPUT_9, and_43_out);
  and and_45 (and_45_out, OUTPUT_10, and_44_out);
  and and_46 (and_46_out, OUTPUT_11, and_45_out);
  and and_47 (and_47_out, OUTPUT_12, and_46_out);
  and and_48 (and_48_out, OUTPUT_13, and_47_out);
  and and_49 (and_49_out, OUTPUT_14, and_48_out);
  L_1_Bit_B_Reg l_1_bit_b_reg_1 (
    .J1(and_2_out), .J2(and_3_out), .K1(CLR), .K2(and_2_out), .K3(and_4_out), .CLK(CLK), .OUTPUT(OUTPUT_0));
  L_1_Bit_B_Reg l_1_bit_b_reg_2 (
    .J1(and_35_out), .J2(and_5_out), .K1(CLR), .K2(and_35_out), .K3(and_6_out), .CLK(CLK), .OUTPUT(OUTPUT_1));
  L_1_Bit_B_Reg l_1_bit_b_reg_3 (
    .J1(and_36_out), .J2(and_7_out), .K1(CLR), .K2(and_36_out), .K3(and_8_out), .CLK(CLK), .OUTPUT(OUTPUT_2));
  L_1_Bit_B_Reg l_1_bit_b_reg_4 (
    .J1(and_37_out), .J2(and_9_out), .K1(CLR), .K2(and_37_out), .K3(and_10_out), .CLK(CLK), .OUTPUT(OUTPUT_3));
  L_1_Bit_B_Reg l_1_bit_b_reg_5 (
    .J1(and_38_out), .J2(and_11_out), .K1(CLR), .K2(and_38_out), .K3(and_12_out), .CLK(CLK), .OUTPUT(OUTPUT_4));
  L_1_Bit_B_Reg l_1_bit_b_reg_6 (
    .J1(and_39_out), .J2(and_13_out), .K1(CLR), .K2(and_39_out), .K3(and_14_out), .CLK(CLK), .OUTPUT(OUTPUT_5));
  L_1_Bit_B_Reg l_1_bit_b_reg_7 (
    .J1(and_40_out), .J2(and_15_out), .K1(CLR), .K2(and_40_out), .K3(and_16_out), .CLK(CLK), .OUTPUT(OUTPUT_6));
  L_1_Bit_B_Reg l_1_bit_b_reg_8 (
    .J1(and_41_out), .J2(and_17_out), .K1(CLR), .K2(and_41_out), .K3(and_18_out), .CLK(CLK), .OUTPUT(OUTPUT_7));
  L_1_Bit_B_Reg l_1_bit_b_reg_9 (
    .J1(and_42_out), .J2(and_19_out), .K1(CLR), .K2(and_42_out), .K3(and_20_out), .CLK(CLK), .OUTPUT(OUTPUT_8));
  L_1_Bit_B_Reg l_1_bit_b_reg_10 (
    .J1(and_43_out), .J2(and_21_out), .K1(CLR), .K2(and_43_out), .K3(and_22_out), .CLK(CLK), .OUTPUT(OUTPUT_9));
  L_1_Bit_B_Reg l_1_bit_b_reg_11 (
    .J1(and_44_out), .J2(and_23_out), .K1(CLR), .K2(and_44_out), .K3(and_24_out), .CLK(CLK),
    .OUTPUT(OUTPUT_10));
  L_1_Bit_B_Reg l_1_bit_b_reg_12 (
    .J1(and_45_out), .J2(and_25_out), .K1(CLR), .K2(and_45_out), .K3(and_26_out), .CLK(CLK),
    .OUTPUT(OUTPUT_11));
  L_1_Bit_B_Reg l_1_bit_b_reg_13 (
    .J1(and_46_out), .J2(and_27_out), .K1(CLR), .K2(and_46_out), .K3(and_28_out), .CLK(CLK),
    .OUTPUT(OUTPUT_12));
  L_1_Bit_B_Reg l_1_bit_b_reg_14 (
    .J1(and_47_out), .J2(and_29_out), .K1(CLR), .K2(and_47_out), .K3(and_30_out), .CLK(CLK),
    .OUTPUT(OUTPUT_13));
  L_1_Bit_B_Reg l_1_bit_b_reg_15 (
    .J1(and_48_out), .J2(and_31_out), .K1(CLR), .K2(and_48_out), .K3(and_32_out), .CLK(CLK),
    .OUTPUT(OUTPUT_14));
  L_1_Bit_B_Reg l_1_bit_b_reg_16 (
    .J1(and_49_out), .J2(and_33_out), .K1(CLR), .K2(and_49_out), .K3(and_34_out), .CLK(CLK),
    .OUTPUT(OUTPUT_15));
endmodule

// 16-Bit BUS
module L_16_Bit_BUS (
);

  wire l_1_ortak_bus_1_output_5, l_1_ortak_bus_1_output_6, l_1_ortak_bus_2_output_5,
       l_1_ortak_bus_2_output_6, l_1_ortak_bus_3_output_5, l_1_ortak_bus_3_output_6,
       l_1_ortak_bus_4_output_5, l_1_ortak_bus_4_output_6, l_1_ortak_bus_5_output_5,
       l_1_ortak_bus_5_output_6, l_1_ortak_bus_6_output_5, l_1_ortak_bus_6_output_6,
       l_1_ortak_bus_7_output_5, l_1_ortak_bus_7_output_6, l_1_ortak_bus_8_output_5,
       l_1_ortak_bus_8_output_6, l_1_ortak_bus_9_output_5, l_1_ortak_bus_9_output_6,
       l_1_ortak_bus_10_output_5, l_1_ortak_bus_10_output_6, l_1_ortak_bus_11_output_5,
       l_1_ortak_bus_11_output_6, l_1_ortak_bus_12_output_5, l_1_ortak_bus_12_output_6,
       l_1_ortak_bus_13_output_5, l_1_ortak_bus_13_output_6, l_1_ortak_bus_14_output_5,
       l_1_ortak_bus_14_output_6, l_1_ortak_bus_15_output_4, l_1_ortak_bus_15_output_5,
       l_1_ortak_bus_15_output_6;
  wire [2:0] l_1_ortak_bus_1_select;

  L_1_Ortak_BUS l_1_ortak_bus_1 (
    .Select(l_1_ortak_bus_1_select), .Output_5(l_1_ortak_bus_1_output_5), .Output_6(l_1_ortak_bus_1_output_6));  // open: Output_0, Output_1, Output_2, Input_0, Input_1, Input_2, Input_3, Input_4, Input_5, Input_6, Input_7, Output_3, Output_4, Output_7
  L_1_Ortak_BUS l_1_ortak_bus_2 (
    .Output_0(l_1_ortak_bus_1_output_5), .Output_1(l_1_ortak_bus_1_output_6),
    .Select(l_1_ortak_bus_1_select), .Output_5(l_1_ortak_bus_2_output_5), .Output_6(l_1_ortak_bus_2_output_6));  // open: Output_2, Input_0, Input_1, Input_2, Input_3, Input_4, Input_5, Input_6, Input_7, Output_3, Output_4, Output_7
  L_1_Ortak_BUS l_1_ortak_bus_3 (
    .Output_0(l_1_ortak_bus_2_output_5), .Output_1(l_1_ortak_bus_2_output_6),
    .Select(l_1_ortak_bus_1_select), .Output_5(l_1_ortak_bus_3_output_5), .Output_6(l_1_ortak_bus_3_output_6));  // open: Output_2, Input_0, Input_1, Input_2, Input_3, Input_4, Input_5, Input_6, Input_7, Output_3, Output_4, Output_7
  L_1_Ortak_BUS l_1_ortak_bus_4 (
    .Output_0(l_1_ortak_bus_3_output_5), .Output_1(l_1_ortak_bus_3_output_6),
    .Select(l_1_ortak_bus_1_select), .Output_5(l_1_ortak_bus_4_output_5), .Output_6(l_1_ortak_bus_4_output_6));  // open: Output_2, Input_0, Input_1, Input_2, Input_3, Input_4, Input_5, Input_6, Input_7, Output_3, Output_4, Output_7
  L_1_Ortak_BUS l_1_ortak_bus_5 (
    .Output_0(l_1_ortak_bus_4_output_5), .Output_1(l_1_ortak_bus_4_output_6),
    .Select(l_1_ortak_bus_1_select), .Output_5(l_1_ortak_bus_5_output_5), .Output_6(l_1_ortak_bus_5_output_6));  // open: Output_2, Input_0, Input_1, Input_2, Input_3, Input_4, Input_5, Input_6, Input_7, Output_3, Output_4, Output_7
  L_1_Ortak_BUS l_1_ortak_bus_6 (
    .Output_0(l_1_ortak_bus_5_output_5), .Output_1(l_1_ortak_bus_5_output_6),
    .Select(l_1_ortak_bus_1_select), .Output_5(l_1_ortak_bus_6_output_5), .Output_6(l_1_ortak_bus_6_output_6));  // open: Output_2, Input_0, Input_1, Input_2, Input_3, Input_4, Input_5, Input_6, Input_7, Output_3, Output_4, Output_7
  L_1_Ortak_BUS l_1_ortak_bus_7 (
    .Output_0(l_1_ortak_bus_6_output_5), .Output_1(l_1_ortak_bus_6_output_6),
    .Select(l_1_ortak_bus_1_select), .Output_5(l_1_ortak_bus_7_output_5), .Output_6(l_1_ortak_bus_7_output_6));  // open: Output_2, Input_0, Input_1, Input_2, Input_3, Input_4, Input_5, Input_6, Input_7, Output_3, Output_4, Output_7
  L_1_Ortak_BUS l_1_ortak_bus_8 (
    .Output_0(l_1_ortak_bus_7_output_5), .Output_1(l_1_ortak_bus_7_output_6),
    .Select(l_1_ortak_bus_1_select), .Output_5(l_1_ortak_bus_8_output_5), .Output_6(l_1_ortak_bus_8_output_6));  // open: Output_2, Input_0, Input_1, Input_2, Input_3, Input_4, Input_5, Input_6, Input_7, Output_3, Output_4, Output_7
  L_1_Ortak_BUS l_1_ortak_bus_9 (
    .Output_0(l_1_ortak_bus_8_output_5), .Output_1(l_1_ortak_bus_8_output_6),
    .Select(l_1_ortak_bus_1_select), .Output_5(l_1_ortak_bus_9_output_5), .Output_6(l_1_ortak_bus_9_output_6));  // open: Output_2, Input_0, Input_1, Input_2, Input_3, Input_4, Input_5, Input_6, Input_7, Output_3, Output_4, Output_7
  L_1_Ortak_BUS l_1_ortak_bus_10 (
    .Output_0(l_1_ortak_bus_9_output_5), .Output_1(l_1_ortak_bus_9_output_6),
    .Select(l_1_ortak_bus_1_select), .Output_5(l_1_ortak_bus_10_output_5),
    .Output_6(l_1_ortak_bus_10_output_6));  // open: Output_2, Input_0, Input_1, Input_2, Input_3, Input_4, Input_5, Input_6, Input_7, Output_3, Output_4, Output_7
  L_1_Ortak_BUS l_1_ortak_bus_11 (
    .Output_0(l_1_ortak_bus_10_output_5), .Output_1(l_1_ortak_bus_10_output_6),
    .Select(l_1_ortak_bus_1_select), .Output_5(l_1_ortak_bus_11_output_5),
    .Output_6(l_1_ortak_bus_11_output_6));  // open: Output_2, Input_0, Input_1, Input_2, Input_3, Input_4, Input_5, Input_6, Input_7, Output_3, Output_4, Output_7
  L_1_Ortak_BUS l_1_ortak_bus_12 (
    .Output_0(l_1_ortak_bus_11_output_5), .Output_1(l_1_ortak_bus_11_output_6),
    .Select(l_1_ortak_bus_1_select), .Output_5(l_1_ortak_bus_12_output_5),
    .Output_6(l_1_ortak_bus_12_output_6));  // open: Output_2, Input_0, Input_1, Input_2, Input_3, Input_4, Input_5, Input_6, Input_7, Output_3, Output_4, Output_7
  L_1_Ortak_BUS l_1_ortak_bus_13 (
    .Output_0(l_1_ortak_bus_12_output_5), .Output_1(l_1_ortak_bus_12_output_6),
    .Select(l_1_ortak_bus_1_select), .Output_5(l_1_ortak_bus_13_output_5),
    .Output_6(l_1_ortak_bus_13_output_6));  // open: Output_2, Input_0, Input_1, Input_2, Input_3, Input_4, Input_5, Input_6, Input_7, Output_3, Output_4, Output_7
  L_1_Ortak_BUS l_1_ortak_bus_14 (
    .Output_0(l_1_ortak_bus_13_output_5), .Output_1(l_1_ortak_bus_13_output_6),
    .Select(l_1_ortak_bus_1_select), .Output_5(l_1_ortak_bus_14_output_5),
    .Output_6(l_1_ortak_bus_14_output_6));  // open: Output_2, Input_0, Input_1, Input_2, Input_3, Input_4, Input_5, Input_6, Input_7, Output_3, Output_4, Output_7
  L_1_Ortak_BUS l_1_ortak_bus_15 (
    .Output_0(l_1_ortak_bus_14_output_5), .Output_1(l_1_ortak_bus_14_output_6),
    .Select(l_1_ortak_bus_1_select), .Output_4(l_1_ortak_bus_15_output_4),
    .Output_5(l_1_ortak_bus_15_output_5), .Output_6(l_1_ortak_bus_15_output_6));  // open: Output_2, Input_0, Input_1, Input_2, Input_3, Input_4, Input_5, Input_6, Input_7, Output_3, Output_7
  L_1_Ortak_BUS l_1_ortak_bus_16 (
    .Output_0(l_1_ortak_bus_15_output_4), .Output_1(l_1_ortak_bus_15_output_5),
    .Output_2(l_1_ortak_bus_15_output_6), .Select(l_1_ortak_bus_1_select));  // open: Input_0, Input_1, Input_2, Input_3, Input_4, Input_5, Input_6, Input_7, Output_3, Output_4, Output_5, Output_6, Output_7
  AR ar_1 ();  // open: CLK, I, R, T0, T2, T3, T4, D7, D5, INPUT, OUTPUT
endmodule

module AR (
  input  CLK,
  input  I,
  input  R,
  input  T0,
  input  T2,
  input  T3,
  input  T4,
  input  D7,
  input  D5,
  input  [11:0] INPUT,
  output [11:0] OUTPUT
);

  wire and_1_out, and_2_out, and_3_out, and_4_out, and_5_out, or_1_out;

  and and_1 (and_1_out, R, T0);
  and and_2 (and_2_out, ~R, T0);  // AND_Gate
  and and_3 (and_3_out, ~R, T2);  // AND_Gate
  and and_4 (and_4_out, I, T3, ~D7);  // AND_Gate
  and and_5 (and_5_out, T4, D5);
  or or_1 (or_1_out, and_2_out, and_3_out, and_4_out);
  L_12_Bit_A_Register L_12_Bit_A_Register_1 (
    .CLR(and_1_out), .LD(or_1_out), .INC(and_5_out), .INPUT_0(INPUT[0]), .INPUT_1(INPUT[1]),
    .INPUT_2(INPUT[2]), .INPUT_3(INPUT[3]), .INPUT_4(INPUT[4]), .INPUT_5(INPUT[5]), .INPUT_6(INPUT[6]),
    .INPUT_7(INPUT[7]), .INPUT_8(INPUT[8]), .INPUT_9(INPUT[9]), .INPUT_10(INPUT[10]), .INPUT_11(INPUT[11]),
    .CLK(CLK), .OUTPUT_0(OUTPUT[0]), .OUTPUT_1(OUTPUT[1]), .OUTPUT_2(OUTPUT[2]), .OUTPUT_3(OUTPUT[3]),
    .OUTPUT_4(OUTPUT[4]), .OUTPUT_5(OUTPUT[5]), .OUTPUT_6(OUTPUT[6]), .OUTPUT_7(OUTPUT[7]),
    .OUTPUT_8(OUTPUT[8]), .OUTPUT_9(OUTPUT[9]), .OUTPUT_10(OUTPUT[10]), .OUTPUT_11(OUTPUT[11]));  // open: Cout

  // Notes on the sheet:
  //   CLR=R*T0
  //   R'*T0
  //   D7'*I*T3
  //   INC=D5*T4
  //   LD=R'*T0+R'*T2+D7'*I*T3
endmodule

module PC (
  input  CLK,
  input  AC_15,
  input  AC_0,
  input  I,
  input  E,
  input  R,
  input  IEN,
  input  FGI,
  input  FGO,
  input  T1,
  input  T3,
  input  T4,
  input  T5,
  input  D4,
  input  D5,
  input  D7,
  input  B1,
  input  B2,
  input  B3,
  input  B4,
  input  B8,
  input  B9,
  input  [11:0] \input ,
  output [11:0] \output 
);

  wire and_1_out, and_2_out, and_3_out, and_4_out, and_5_out, and_6_out, and_7_out, and_8_out, and_9_out,
       and_10_out, and_11_out, and_12_out, and_13_out, and_14_out, and_15_out, and_16_out, and_17_out,
       not_1_out, not_2_out, not_3_out, or_1_out, or_2_out;

  and and_1 (and_1_out, R, T1);
  and and_2 (and_2_out, T4, D4);
  and and_3 (and_3_out, T5, D5);
  not not_1 (not_1_out, I);
  or or_1 (or_1_out, and_2_out, and_3_out);
  and and_4 (and_4_out, not_1_out, T3, D7);
  not not_2 (not_2_out, AC_15);
  not not_3 (not_3_out, AC_0);
  and and_5 (and_5_out, and_4_out, B4);
  and and_6 (and_6_out, and_4_out, B3);
  and and_7 (and_7_out, and_4_out, B2);
  and and_8 (and_8_out, and_4_out, B1);
  and and_9 (and_9_out, I, T3, D7);
  and and_10 (and_10_out, and_9_out, B8);
  and and_11 (and_11_out, and_5_out, not_2_out);
  and and_12 (and_12_out, and_6_out, AC_15);
  and and_13 (and_13_out, and_7_out, not_3_out);
  and and_14 (and_14_out, and_8_out, E);
  and and_15 (and_15_out, FGI, and_16_out);
  and and_16 (and_16_out, and_9_out, B9);
  and and_17 (and_17_out, FGO, and_10_out);
  or or_2 (or_2_out, and_11_out, and_12_out, and_13_out, and_14_out, and_15_out, and_17_out);
  L_12_Bit_A_Register L_12_Bit_A_Register_1 (
    .CLR(and_1_out), .LD(or_1_out), .INC(or_2_out), .INPUT_0(\input [0]), .INPUT_1(\input [1]),
    .INPUT_2(\input [2]), .INPUT_3(\input [3]), .INPUT_4(\input [4]), .INPUT_5(\input [5]),
    .INPUT_6(\input [6]), .INPUT_7(\input [7]), .INPUT_8(\input [8]), .INPUT_9(\input [9]),
    .INPUT_10(\input [10]), .INPUT_11(\input [11]), .CLK(CLK), .OUTPUT_0(\output [0]),
    .OUTPUT_1(\output [1]), .OUTPUT_2(\output [2]), .OUTPUT_3(\output [3]), .OUTPUT_4(\output [4]),
    .OUTPUT_5(\output [5]), .OUTPUT_6(\output [6]), .OUTPUT_7(\output [7]), .OUTPUT_8(\output [8]),
    .OUTPUT_9(\output [9]), .OUTPUT_10(\output [10]), .OUTPUT_11(\output [11]));  // open: Cout

  // Notes on the sheet:
  //   CLR= R*T1
  //   r=D7 I' T3
  //   p=D7*I*T3
  //   LD=D4*T4+D5*T5
  //   r*B4*AC(15)'
  //   r*B3*AC(15)
  //   r*B2*AC(0)'
  //   r*B1*E
  //   p B9 FGI
  //   p B8 FG0
  //   DR'D6T6p girişi için tekrar kontrol et
  //   INC=r*B4*AC(15)'+r*B3*AC(15)+r*B2*AC(0)'+r*B1*E+p*B9*FGI +p*B8*FG0
endmodule

module DR (
  input  CLK,
  input  T4,
  input  T5,
  input  T6,
  input  D0,
  input  D1,
  input  D2,
  input  D6,
  input  [15:0] Input,
  output [15:0] \output 
);

  wire and_1_out, and_2_out, or_1_out;

  or or_1 (or_1_out, D0, D1, D2, D6);
  and and_1 (and_1_out, T5, D6);
  and and_2 (and_2_out, T4, or_1_out);
  L_16_Bit_A_Register L_16_Bit_A_Register_1 (
    .CLR(1'b0), .LD(and_2_out), .INC(and_1_out), .INPUT_0(Input[0]), .INPUT_1(Input[1]), .INPUT_2(Input[2]),
    .INPUT_3(Input[3]), .INPUT_4(Input[4]), .INPUT_5(Input[5]), .INPUT_6(Input[6]), .INPUT_7(Input[7]),
    .INPUT_8(Input[8]), .INPUT_9(Input[9]), .INPUT_10(Input[10]), .INPUT_11(Input[11]), .INPUT_12(Input[12]),
    .INPUT_13(Input[13]), .INPUT_14(Input[14]), .INPUT_15(Input[15]), .CLK(CLK), .OUTPUT_0(\output [0]),
    .OUTPUT_1(\output [1]), .OUTPUT_2(\output [2]), .OUTPUT_3(\output [3]), .OUTPUT_4(\output [4]),
    .OUTPUT_5(\output [5]), .OUTPUT_6(\output [6]), .OUTPUT_7(\output [7]), .OUTPUT_8(\output [8]),
    .OUTPUT_9(\output [9]), .OUTPUT_10(\output [10]), .OUTPUT_11(\output [11]), .OUTPUT_12(\output [12]),
    .OUTPUT_13(\output [13]), .OUTPUT_14(\output [14]), .OUTPUT_15(\output [15]));  // open: Eout

  // Notes on the sheet:
  //   INC= D6 T5
  //   LD= (D0+D1+D2+D6)*T4
endmodule

module TR (
  input  CLK,
  input  R,
  input  IEN,
  input  FGI,
  input  FGO,
  input  T0,
  input  [15:0] \input ,
  output [15:0] \output 
);

  wire and_1_out;

  and and_1 (and_1_out, R, T0);
  L_16_Bit_A_Register L_16_Bit_A_Register_1 (
    .CLR(1'b0), .LD(and_1_out), .INC(1'b0), .INPUT_0(\input [0]), .INPUT_1(\input [1]), .INPUT_2(\input [2]),
    .INPUT_3(\input [3]), .INPUT_4(\input [4]), .INPUT_5(\input [5]), .INPUT_6(\input [6]),
    .INPUT_7(\input [7]), .INPUT_8(\input [8]), .INPUT_9(\input [9]), .INPUT_10(\input [10]),
    .INPUT_11(\input [11]), .INPUT_12(\input [12]), .INPUT_13(\input [13]), .INPUT_14(\input [14]),
    .INPUT_15(\input [15]), .CLK(CLK), .OUTPUT_0(\output [0]), .OUTPUT_1(\output [1]),
    .OUTPUT_2(\output [2]), .OUTPUT_3(\output [3]), .OUTPUT_4(\output [4]), .OUTPUT_5(\output [5]),
    .OUTPUT_6(\output [6]), .OUTPUT_7(\output [7]), .OUTPUT_8(\output [8]), .OUTPUT_9(\output [9]),
    .OUTPUT_10(\output [10]), .OUTPUT_11(\output [11]), .OUTPUT_12(\output [12]), .OUTPUT_13(\output [13]),
    .OUTPUT_14(\output [14]), .OUTPUT_15(\output [15]));  // open: Eout

  // Notes on the sheet:
  //   LD= R T0
endmodule

// IR REG
module IR (
  input  CLK,
  input  R,
  input  T1,
  input  [15:0] \input ,
  output IR_15,
  output [15:0] \output 
);

  wire and_1_out, not_1_out;

  not not_1 (not_1_out, R);
  and and_1 (and_1_out, not_1_out, T1);
  L_16_Bit_A_Register L_16_Bit_A_Register_12a9343c_1 (
    .CLR(1'b0), .LD(and_1_out), .INC(1'b0), .INPUT_0(\input [0]), .INPUT_1(\input [1]), .INPUT_2(\input [2]),
    .INPUT_3(\input [3]), .INPUT_4(\input [4]), .INPUT_5(\input [5]), .INPUT_6(\input [6]),
    .INPUT_7(\input [7]), .INPUT_8(\input [8]), .INPUT_9(\input [9]), .INPUT_10(\input [10]),
    .INPUT_11(\input [11]), .INPUT_12(\input [12]), .INPUT_13(\input [13]), .INPUT_14(\input [14]),
    .INPUT_15(\input [15]), .CLK(CLK), .OUTPUT_0(\output [0]), .OUTPUT_1(\output [1]),
    .OUTPUT_2(\output [2]), .OUTPUT_3(\output [3]), .OUTPUT_4(\output [4]), .OUTPUT_5(\output [5]),
    .OUTPUT_6(\output [6]), .OUTPUT_7(\output [7]), .OUTPUT_8(\output [8]), .OUTPUT_9(\output [9]),
    .OUTPUT_10(\output [10]), .OUTPUT_11(\output [11]), .OUTPUT_12(\output [12]), .OUTPUT_13(\output [13]),
    .OUTPUT_14(\output [14]), .OUTPUT_15(IR_15));  // open: Eout

  assign \output [15] = IR_15;

  // Notes on the sheet:
  //   LD=R' T1 
endmodule

module OUTR (
  input  CLK,
  input  I,
  input  T3,
  input  D7,
  input  B10,
  input  [7:0] \input ,
  output [7:0] \output 
);

  wire and_1_out, and_2_out;

  and and_1 (and_1_out, I, T3, D7);
  and and_2 (and_2_out, and_1_out, B10);
  L_8_Bit_B_Reg L_8_Bit_B_Reg_1 (
    .CLR(1'b0), .LD(and_2_out), .INC(1'b0), .INPUT_0(\input [0]), .INPUT_1(\input [1]), .INPUT_2(\input [2]),
    .INPUT_3(\input [3]), .INPUT_4(\input [4]), .INPUT_5(\input [5]), .INPUT_6(\input [6]),
    .INPUT_7(\input [7]), .CLK(CLK), .OUTPUT_0(\output [0]), .OUTPUT_1(\output [1]), .OUTPUT_2(\output [2]),
    .OUTPUT_3(\output [3]), .OUTPUT_4(\output [4]), .OUTPUT_5(\output [5]), .OUTPUT_6(\output [6]),
    .OUTPUT_7(\output [7]));

  // Notes on the sheet:
  //   LD= D7 I T3 B(10)
endmodule

module INPR (
  input  CLK,
  input  [7:0] \input ,
  output [7:0] \output 
);

  L_8_Bit_B_Reg L_8_Bit_B_Reg_1 (
    .CLR(1'b0), .LD(1'b0), .INC(1'b0), .INPUT_0(\input [0]), .INPUT_1(\input [1]), .INPUT_2(\input [2]),
    .INPUT_3(\input [3]), .INPUT_4(\input [4]), .INPUT_5(\input [5]), .INPUT_6(\input [6]),
    .INPUT_7(\input [7]), .CLK(CLK), .OUTPUT_0(\output [0]), .OUTPUT_1(\output [1]), .OUTPUT_2(\output [2]),
    .OUTPUT_3(\output [3]), .OUTPUT_4(\output [4]), .OUTPUT_5(\output [5]), .OUTPUT_6(\output [6]),
    .OUTPUT_7(\output [7]));
endmodule

module Memory (
  input  [11:0] Address,
  input  CLK,
  input  I,
  input  R,
  input  T1,
  input  T3,
  input  T4,
  input  T6,
  input  D0,
  input  D1,
  input  D2,
  input  D3,
  input  D5,
  input  D6,
  input  D7,
  input  [15:0] DATA_IN,
  output [15:0] DATA_OUT
);

  wire and_1_out, and_2_out, and_3_out, and_4_out, and_5_out, and_6_out, and_7_out, or_1_out, or_2_out,
       or_3_out;

  and and_1 (and_1_out, I, T3, ~D7);  // AND_Gate
  and and_2 (and_2_out, ~R, T1);  // AND_Gate
  and and_3 (and_3_out, T4, or_1_out);
  or or_1 (or_1_out, D2, D0, D1, D6);
  and and_4 (and_4_out, R, T1);
  and and_5 (and_5_out, T3, D3);
  and and_6 (and_6_out, T4, D5);
  and and_7 (and_7_out, T6, D6);
  or or_2 (or_2_out, and_4_out, and_5_out, and_6_out, and_7_out);
  or or_3 (or_3_out, and_2_out, and_1_out, and_3_out);
  RAM #(.addrWidth(12), .dataWidth(16)) ram_1 (
    .addr(Address), .data(DATA_OUT), .clk(CLK), .ld(or_3_out));  // open: sel, clr

  // Notes on the sheet:
  //   R T1
  //   D3 T3
  //    D7' I T3 
  //   D5 T4
  //   D6 T6
  //   R' T1
  //   (D0+D1+D6+D2)*T4
  //   MemRead=R' T1 + D7' I T3 + T4* (D0 + D1 + D2 +D6)
  //   MemWrt= R T1 + D3 T4 + D5 T4 + D6 T6
endmodule

module AC (
  input  CLK,
  input  I,
  input  E,
  input  T3,
  input  T4,
  input  T5,
  input  D0,
  input  D1,
  input  D2,
  input  D7,
  input  B5,
  input  B6,
  input  B7,
  input  [15:0] INPUT,
  input  B9,
  input  B11,
  output AC_0,
  output AC_15,
  output [15:0] OUTPUT,
  output LD,
  output AND,
  output ADD,
  output DR,
  output INPR,
  output COM,
  output SHR,
  output SHL
);

  wire and_1_out, and_5_out, and_6_out, and_11_out;

  and and_1 (and_1_out, I, T3, D7);
  and and_2 (AND, T5, D0);
  and and_3 (ADD, T5, D1);
  and and_4 (DR, T5, D2);
  and and_5 (and_5_out, ~I, D7, T3);  // AND_Gate
  and and_6 (and_6_out, B11, and_5_out);
  and and_7 (COM, and_5_out, B9);
  and and_8 (SHR, and_5_out, B7);
  and and_9 (SHL, and_5_out, B6);
  and and_10 (INPR, and_1_out, B11);
  and and_11 (and_11_out, B5, and_5_out);
  or or_1 (LD, COM, SHR, SHL, INPR, AND, ADD, DR);
  L_16_Bit_A_Register L_16_Bit_A_Register_1 (
    .CLR(and_6_out), .LD(LD), .INC(and_11_out), .INPUT_0(INPUT[0]), .INPUT_1(INPUT[1]), .INPUT_2(INPUT[2]),
    .INPUT_3(INPUT[3]), .INPUT_4(INPUT[4]), .INPUT_5(INPUT[5]), .INPUT_6(INPUT[6]), .INPUT_7(INPUT[7]),
    .INPUT_8(INPUT[8]), .INPUT_9(INPUT[9]), .INPUT_10(INPUT[10]), .INPUT_11(INPUT[11]), .INPUT_12(INPUT[12]),
    .INPUT_13(INPUT[13]), .INPUT_14(INPUT[14]), .INPUT_15(INPUT[15]), .CLK(CLK), .OUTPUT_0(AC_0),
    .OUTPUT_1(OUTPUT[1]), .OUTPUT_2(OUTPUT[2]), .OUTPUT_3(OUTPUT[3]), .OUTPUT_4(OUTPUT[4]),
    .OUTPUT_5(OUTPUT[5]), .OUTPUT_6(OUTPUT[6]), .OUTPUT_7(OUTPUT[7]), .OUTPUT_8(OUTPUT[8]),
    .OUTPUT_9(OUTPUT[9]), .OUTPUT_10(OUTPUT[10]), .OUTPUT_11(OUTPUT[11]), .OUTPUT_12(OUTPUT[12]),
    .OUTPUT_13(OUTPUT[13]), .OUTPUT_14(OUTPUT[14]), .OUTPUT_15(AC_15), .Eout(E));

  assign {OUTPUT[15], OUTPUT[0]} = {AC_15, AC_0};

  // Notes on the sheet:
  //   r=D7*I'*T3
  //   p=D7*I*T3
  //   D0*T5
  //   D1*T5
  //   D2*T5
  //   r*B9
  //   r*B7
  //   SHR
  //   SHL
  //   r*B6
  //   COM
  //   p*B11
  //   INPR
  //   AND
  //   ADD
  //   DR
  //   CLR=r*B11
  //   INC=r*B5
  //   LD=D0*T5+D1*T5+D2*T5+p*B11+r*B9+r*B7+r*B6
endmodule

// FLAG I
module FLAG_I (
  input  CLK,
  input  IR_15,
  input  R,
  input  T2,
  output I
);

  wire and_1_out, and_2_out;

  and and_1 (and_1_out, ~R, T2);  // AND_Gate
  and and_2 (and_2_out, IR_15, and_1_out);
  D_Flip_Flop d_ff_1 (.clk(CLK), .D(and_2_out), .Q(I));  // open: Qn, preset, en, reset

  // Notes on the sheet:
  //   I = R' T2 IR(15)
endmodule

module FLAG_S (
  input  CLK,
  input  I,
  input  T3,
  input  D7,
  input  B0,
  output S
);

  wire and_1_out, and_2_out;

  and and_1 (and_1_out, ~I, T3, D7);  // AND_Gate
  and and_2 (and_2_out, and_1_out, B0);
  D_Flip_Flop d_ff_1 (.clk(CLK), .D(and_2_out), .Q(S));  // open: Qn, preset, en, reset

  // Notes on the sheet:
  //   S= D7 I' T3 B(0)
endmodule

module FLAG_R (
  input  CLK,
  input  IEN,
  input  FGI,
  input  FGO,
  input  T0,
  input  T1,
  input  T2,
  output R
);

  wire and_1_out, and_2_out, and_3_out, not_1_out, not_2_out, not_3_out, or_1_out;

  not not_1 (not_1_out, T0);
  not not_2 (not_2_out, T1);
  not not_3 (not_3_out, T2);
  or or_1 (or_1_out, FGI, FGO);
  and and_1 (and_1_out, not_1_out, not_2_out, not_3_out);
  and and_2 (and_2_out, IEN, or_1_out, and_1_out);
  and and_3 (and_3_out, T2, R);
  J_K_Flip_Flop j_k_ff_1 (.J(and_2_out), .clk(CLK), .K(and_3_out), .Q(R));  // open: Qn, preset, en, reset

  // Notes on the sheet:
  //   R T2
endmodule

module FLAG_IEN (
  input  CLK,
  input  I,
  input  R,
  input  T2,
  input  T3,
  input  D7,
  input  B6,
  input  B7,
  output IEN
);

  wire and_1_out, and_2_out, and_3_out, and_4_out, or_1_out;

  and and_1 (and_1_out, I, T3, D7);
  and and_2 (and_2_out, and_1_out, B7);
  and and_3 (and_3_out, and_1_out, B6);
  and and_4 (and_4_out, R, T2);
  J_K_Flip_Flop j_k_ff_1 (.J(and_2_out), .clk(CLK), .K(or_1_out), .Q(IEN));  // open: Qn, preset, en, reset
  or or_1 (or_1_out, and_3_out, and_4_out);

  // Notes on the sheet:
  //   p= D7 I T3
  //   p B(7)
  //   R T2 + B(6) p
endmodule

module FGI (
  input  CLK,
  input  I,
  input  T3,
  input  D7,
  input  B11,
  output FGI
);

  wire and_1_out, and_2_out;

  and and_1 (and_1_out, I, T3, D7);
  and and_2 (and_2_out, and_1_out, B11);
  D_Flip_Flop d_ff_1 (.clk(CLK), .D(and_2_out), .Q(FGI));  // open: Qn, preset, en, reset

  // Notes on the sheet:
  //   D7 I T3 B(11)
endmodule

module FGO (
  input  CLK,
  input  I,
  input  T3,
  input  D7,
  input  B10,
  output FGO
);

  wire and_1_out, and_2_out;

  and and_1 (and_1_out, I, T3, D7);
  and and_2 (and_2_out, and_1_out, B10);
  D_Flip_Flop d_ff_1 (.clk(CLK), .D(and_2_out), .Q(FGO));  // open: Qn, preset, en, reset

  // Notes on the sheet:
  //   D7 I T3 B(10)
endmodule

module FLAG_E (
  input  CLK,
  input  Cout,
  input  AC_15,
  input  AC_0,
  input  I,
  input  B6,
  input  B7,
  input  B8,
  input  B10,
  input  T3,
  input  T5,
  input  D1,
  input  D7,
  output E
);

  wire and_1_out, and_2_out, and_3_out, and_4_out, and_5_out, and_6_out, and_7_out, d_ff_1_qn, or_1_out,
       or_2_out;

  and and_1 (and_1_out, ~I, T3, D7);  // AND_Gate
  or or_1 (or_1_out, d_ff_1_qn, Cout, AC_15, AC_0);
  and and_2 (and_2_out, and_1_out, B6);
  and and_3 (and_3_out, B7, and_1_out);
  and and_4 (and_4_out, B8, and_1_out);
  and and_5 (and_5_out, T5, D1);
  and and_6 (and_6_out, and_1_out, B10);
  or or_2 (or_2_out, and_3_out, and_2_out, and_4_out, and_5_out);
  and and_7 (and_7_out, or_1_out, or_2_out);
  D_Flip_Flop d_ff_1 (.clk(CLK), .D(and_7_out), .Q(E), .Qn(d_ff_1_qn), .reset(and_6_out));  // open: preset, en

  // Notes on the sheet:
  //   r=D7 I' T3
  //   CLR= r B(10) 
  //   Load=D1 T5 + r B7 + r B6 + r B8
  //   Input= AC(0) + AC(15) + C0 + E'
endmodule

// 7x3 encoder
module L_7X3_Encoder (
  input  x1,
  input  x2,
  input  x3,
  input  x4,
  input  x5,
  input  x6,
  input  x7,
  output s0,
  output s1,
  output s2
);

  or or_1 (s0, x1, x3, x5, x7);
  or or_2 (s1, x2, x3, x6, x7);
  or or_3 (s2, x4, x5, x6, x7);
endmodule

// bus select
module BUS_SELEC (
  input  I,
  input  R,
  input  T0,
  input  T1,
  input  T2,
  input  T3,
  input  T4,
  input  T5,
  input  T6,
  input  D0,
  input  D1,
  input  D2,
  input  D3,
  input  D4,
  input  D5,
  input  D6,
  input  D7,
  output [2:0] out_18
);

  wire and_1_out, and_2_out, and_3_out, and_4_out, and_5_out, and_6_out, and_7_out, and_8_out, and_9_out,
       and_10_out, and_11_out, and_12_out, and_13_out, or_1_out, or_2_out, or_3_out, or_4_out, or_5_out;

  and and_1 (and_1_out, T4, D4);
  and and_2 (and_2_out, T5, D5);
  and and_3 (and_3_out, ~R, T0);  // AND_Gate
  and and_4 (and_4_out, T4, D5);
  and and_5 (and_5_out, T5, D2);
  and and_6 (and_6_out, T6, D6);
  and and_7 (and_7_out, R, T0);
  or or_1 (or_1_out, and_1_out, and_2_out);
  or or_2 (or_2_out, and_3_out, and_7_out, and_4_out);
  or or_3 (or_3_out, and_5_out, and_6_out);
  and and_8 (and_8_out, ~R, T2);  // AND_Gate
  and and_9 (and_9_out, I, T3, D7);
  and and_10 (and_10_out, T4, or_4_out);
  or or_4 (or_4_out, D0, D2, D1, D6);
  and and_11 (and_11_out, R, T1);
  and and_12 (and_12_out, T4, D3);
  and and_13 (and_13_out, ~R, T1);  // AND_Gate
  or or_5 (or_5_out, and_13_out, and_9_out, and_10_out);
  L_7X3_Encoder L_7X3_Encoder_1 (
    .x1(or_1_out), .x2(or_2_out), .x3(or_3_out), .x4(and_12_out), .x5(and_8_out), .x6(and_11_out),
    .x7(or_5_out), .s0(out_18[0]), .s1(out_18[1]), .s2(out_18[2]));

  // Notes on the sheet:
  //   AC= D3*T4
  //   IR= R’*T2
  //   TR= R*T1
  //   AR=D4*T4+D5*T5
  //   PC= R’*T0 + RT0 + D5*T4 
  //   DR= D2*T5 + D6*T6
  //   MemRead= R’*T1+D7'*I*T3+T4*(D0+D1+D2+D6)
endmodule

// Control Unit
module Control_Unit (
  input  CLK,
  input  FLAG_I,
  input  FLAG_R,
  input  [15:0] IR_IN,
  input  SC_INC,
  output D0,
  output D1,
  output D2,
  output D3,
  output D4,
  output D5,
  output D6,
  output D7,
  output I,
  output T0,
  output T1,
  output T2,
  output T3,
  output T4,
  output T5,
  output T6,
  output T7,
  output T8,
  output T9,
  output T10,
  output T11,
  output T12,
  output T13,
  output T14,
  output T15
);

  wire and_1_out, and_2_out, and_3_out, and_4_out, and_5_out, and_6_out, and_7_out, and_8_out, and_9_out,
       and_10_out, and_11_out, and_12_out, and_13_out, D0T5_out, D1T5_out, D2T5_out, D3T4_out, D4R4_out,
       D5T5_out, D6T6_out, D7IT3_2_out, D7IT3_out, ir_1_ir_15, or_1_out, or_2_out, or_3_out, or_4_out,
       or_5_out, or_6_out, or_7_out, or_8_out, or_9_out, RT2_out;
  wire [3:0] j_k_ff_1_q;
  wire [15:0] ir_1_output;

  and and_1 (and_1_out, ~or_9_out, 1'b0);  // AND_Gate
  and and_2 (and_2_out, ~or_9_out, ~1'b0, SC_INC);  // AND_Gate
  and and_3 (and_3_out, and_1_out, 1'b0);
  and and_4 (and_4_out, and_1_out, ~1'b0);  // AND_Gate
  and and_5 (and_5_out, and_1_out, 1'b0);
  and and_6 (and_6_out, and_1_out, ~1'b0);  // AND_Gate
  and and_7 (and_7_out, and_1_out, 1'b0);
  and and_8 (and_8_out, and_1_out, ~1'b0);  // AND_Gate
  and and_9 (and_9_out, and_1_out, 1'b0);
  and and_10 (and_10_out, and_1_out, ~1'b0);  // AND_Gate
  or or_1 (or_1_out, and_2_out, and_3_out);
  or or_2 (or_2_out, or_9_out, and_2_out, and_4_out);
  or or_3 (or_3_out, and_11_out, and_5_out);
  or or_4 (or_4_out, or_9_out, and_11_out, and_6_out);
  or or_5 (or_5_out, and_12_out, and_7_out);
  or or_6 (or_6_out, or_9_out, and_12_out, and_8_out);
  or or_7 (or_7_out, and_13_out, and_9_out);
  or or_8 (or_8_out, or_9_out, and_13_out, and_10_out);
  J_K_Flip_Flop j_k_ff_1 (.J(or_1_out), .clk(CLK), .K(or_2_out), .Q(j_k_ff_1_q[0]));  // open: Qn, preset, en, reset
  J_K_Flip_Flop j_k_ff_2 (.J(or_3_out), .clk(CLK), .K(or_4_out), .Q(j_k_ff_1_q[1]));  // open: Qn, preset, en, reset
  J_K_Flip_Flop j_k_ff_3 (.J(or_5_out), .clk(CLK), .K(or_6_out), .Q(j_k_ff_1_q[2]));  // open: Qn, preset, en, reset
  J_K_Flip_Flop j_k_ff_4 (.J(or_7_out), .clk(CLK), .K(or_8_out), .Q(j_k_ff_1_q[3]));  // open: Qn, preset, en, reset
  IR ir_1 (.CLK(CLK), .R(FLAG_R), .T1(T1), .\input (IR_IN), .IR_15(ir_1_ir_15), .\output (ir_1_output));
  and and_11 (and_11_out, j_k_ff_1_q[0], and_2_out);
  and and_12 (and_12_out, j_k_ff_1_q[1], and_11_out);
  and and_13 (and_13_out, j_k_ff_1_q[2], and_12_out);
  Decoder #(.select(4), .enable("false")) decoder_1 (
    .out0(T0), .out1(T1), .out2(T2), .out3(T3), .out4(T4), .out5(T5), .out6(T6), .out7(T7), .out8(T8),
    .out9(T9), .out10(T10), .out11(T11), .out12(T12), .out13(T13), .out14(T14), .out15(T15), .sel(j_k_ff_1_q));
  or or_9 (or_9_out, RT2_out, D0T5_out, D1T5_out, D2T5_out, D3T4_out, D4R4_out, D5T5_out, D6T6_out, D7IT3_out, D7IT3_2_out);
  Decoder #(.select(3), .enable("false")) decoder_2 (
    .out0(D7), .out1(D6), .out2(D5), .out3(D4), .out4(D3), .out5(D2), .out6(D1), .out7(D0),
    .sel(ir_1_output[14:12]));
  FLAG_I flag_i_1 (.CLK(ir_1_output[15]), .IR_15(ir_1_ir_15), .I(I));  // open: R, T2
  and RT2 (RT2_out, T2, FLAG_R);
  and D0T5 (D0T5_out, D0, T5);
  and D1T5 (D1T5_out, D1, T5);
  and D2T5 (D2T5_out, D2, T5);
  and D3T4 (D3T4_out, D3, T4);
  and D4R4 (D4R4_out, D4, T4);
  and D5T5 (D5T5_out, D5, T5);
  and D6T6 (D6T6_out, D6, T6);
  and D7IT3 (D7IT3_out, D7, ~FLAG_I, T3);  // AND_Gate
  and D7IT3_2 (D7IT3_2_out, D7, FLAG_I, T3);

  // Notes on the sheet:
  //   LOAD
  //   CLEAR = RT2 + D0T5 + D1T5 + D2T5 + D3T4 + D4T4 + D5T5 + D6T6 + r + p
  //   OPERATION
  //   TIMING
endmodule

// 1 Bit Bus
module L_1_Ortak_BUS (
  input  Input_0,
  input  Input_1,
  input  Input_2,
  input  Input_3,
  input  Input_4,
  input  Input_5,
  input  Input_6,
  input  Input_7,
  output Output_0,
  output Output_1,
  output Output_2,
  output Output_3,
  output Output_4,
  output Output_5,
  output Output_6,
  output Output_7,
  output [2:0] Select
);

  wire decoder_1_out0, decoder_1_out1, decoder_1_out2, decoder_1_out3, decoder_1_out4, decoder_1_out5,
       decoder_1_out6, decoder_1_out7;

  Decoder #(.select(3), .enable("false")) decoder_1 (
    .out0(decoder_1_out0), .out1(decoder_1_out1), .out2(decoder_1_out2), .out3(decoder_1_out3),
    .out4(decoder_1_out4), .out5(decoder_1_out5), .out6(decoder_1_out6), .out7(decoder_1_out7), .sel(Select));
  assign Output_0 = decoder_1_out0 ? Input_0 : 1'bz;  // Controlled_Buffer controlled_buffer_1
  assign Output_1 = decoder_1_out1 ? Input_1 : 1'bz;  // Controlled_Buffer controlled_buffer_2
  assign Output_2 = decoder_1_out2 ? Input_2 : 1'bz;  // Controlled_Buffer controlled_buffer_3
  assign Output_3 = decoder_1_out3 ? Input_3 : 1'bz;  // Controlled_Buffer controlled_buffer_4
  assign Output_4 = decoder_1_out4 ? Input_4 : 1'bz;  // Controlled_Buffer controlled_buffer_5
  assign Output_5 = decoder_1_out5 ? Input_5 : 1'bz;  // Controlled_Buffer controlled_buffer_6
  assign Output_6 = decoder_1_out6 ? Input_6 : 1'bz;  // Controlled_Buffer controlled_buffer_7
  assign Output_7 = decoder_1_out7 ? Input_7 : 1'bz;  // Controlled_Buffer controlled_buffer_8
endmodule

module ALU (
  input  CLK,
  input  LD,
  input  AND,
  input  ADD,
  input  DR,
  input  INPR,
  input  COM,
  input  SHR,
  input  SHL,
  input  [15:0] AC_INPUT,
  input  [15:0] DR_INPUT,
  input  [7:0] INPR_INPUT,
  output [15:0] OUTPUT,
  output Cout
);

  wire ADD_out, adder_1_cout, adder_1_out, adder_2_cout, adder_2_out, adder_3_cout, adder_3_out,
       adder_4_cout, adder_4_out, adder_5_cout, adder_5_out, adder_6_cout, adder_6_out, adder_7_cout,
       adder_7_out, adder_8_cout, adder_8_out, adder_9_cout, adder_9_out, adder_10_cout, adder_10_out,
       adder_11_cout, adder_11_out, adder_12_cout, adder_12_out, adder_13_cout, adder_13_out, adder_14_cout,
       adder_14_out, adder_15_cout, adder_15_out, adder_16_out, and_1_out, and_2_out, and_3_out, and_4_out,
       and_5_out, and_6_out, and_7_out, and_8_out, and_9_out, and_10_out, and_11_out, and_12_out, and_13_out,
       AND_14_out, and_15_out, and_16_out, and_17_out, and_18_out, and_19_out, and_20_out, and_21_out,
       and_22_out, and_23_out, and_24_out, and_25_out, and_26_out, and_27_out, and_28_out, and_29_out,
       and_30_out, and_31_out, and_32_out, and_33_out, and_34_out, and_35_out, and_36_out, and_37_out,
       and_38_out, and_39_out, and_40_out, and_41_out, and_42_out, and_43_out, and_44_out, and_45_out,
       and_46_out, and_47_out, and_48_out, and_49_out, and_50_out, and_51_out, and_52_out, and_53_out,
       and_54_out, and_55_out, and_56_out, and_57_out, and_58_out, and_59_out, and_60_out, and_61_out,
       and_62_out, and_63_out, and_64_out, and_65_out, and_66_out, and_67_out, and_68_out, and_69_out,
       and_70_out, and_71_out, and_72_out, and_73_out, and_74_out, and_75_out, and_76_out, and_77_out,
       and_78_out, and_79_out, and_80_out, and_81_out, and_82_out, and_83_out, and_84_out, and_85_out,
       and_86_out, and_87_out, and_88_out, and_89_out, and_90_out, and_91_out, and_92_out, and_93_out,
       and_94_out, and_95_out, and_96_out, and_97_out, and_98_out, and_99_out, and_100_out, and_101_out,
       and_102_out, and_103_out, and_104_out, and_105_out, and_106_out, and_107_out, and_108_out,
       and_109_out, and_110_out, and_111_out, and_112_out, and_113_out, and_114_out, and_115_out,
       and_116_out, and_117_out, and_118_out, and_119_out, and_120_out, and_121_out, and_122_out,
       and_123_out, and_124_out, and_125_out, and_126_out, and_127_out, and_128_out, and_129_out,
       and_130_out, COM_out, DR_out, I_0_7a2315b8_out, I_1_b45e6b28_out, I_2_e90cdf88_out, I_3_ffe955a8_out,
       I_4_3525d440_out, I_5_06687591_out, I_6_26eeaca1_out, I_7_1e6fe7d9_out, I_8_9fd21c4f_out,
       I_9_1a6d7d69_out, I_10_95b6212d_out, I_11_758a845c_out, I_12_b38dc382_out, I_13_fca28932_out,
       I_14_c5212871_out, I_15_4d47b025_out, INPR_out, SHL_out, SHR_out;

  Adder #(.width(1)) adder_1 (.a(AC_INPUT[0]), .b(DR_INPUT[0]), .out(adder_1_out), .cin(1'b0), .cout(adder_1_cout));
  Adder #(.width(1)) adder_2 (
    .a(AC_INPUT[1]), .b(DR_INPUT[1]), .out(adder_2_out), .cin(adder_1_cout), .cout(adder_2_cout));
  Adder #(.width(1)) adder_3 (
    .a(AC_INPUT[2]), .b(DR_INPUT[2]), .out(adder_3_out), .cin(adder_2_cout), .cout(adder_3_cout));
  Adder #(.width(1)) adder_4 (
    .a(AC_INPUT[3]), .b(DR_INPUT[3]), .out(adder_4_out), .cin(adder_3_cout), .cout(adder_4_cout));
  Adder #(.width(1)) adder_5 (
    .a(AC_INPUT[4]), .b(DR_INPUT[4]), .out(adder_5_out), .cin(adder_4_cout), .cout(adder_5_cout));
  Adder #(.width(1)) adder_6 (
    .a(AC_INPUT[5]), .b(DR_INPUT[5]), .out(adder_6_out), .cin(adder_5_cout), .cout(adder_6_cout));
  Adder #(.width(1)) adder_7 (
    .a(AC_INPUT[6]), .b(DR_INPUT[6]), .out(adder_7_out), .cin(adder_6_cout), .cout(adder_7_cout));
  Adder #(.width(1)) adder_8 (
    .a(AC_INPUT[7]), .b(DR_INPUT[7]), .out(adder_8_out), .cin(adder_7_cout), .cout(adder_8_cout));
  Adder #(.width(1)) adder_9 (
    .a(AC_INPUT[8]), .b(DR_INPUT[8]), .out(adder_9_out), .cin(adder_8_cout), .cout(adder_9_cout));
  Adder #(.width(1)) adder_10 (
    .a(AC_INPUT[9]), .b(DR_INPUT[9]), .out(adder_10_out), .cin(adder_9_cout), .cout(adder_10_cout));
  Adder #(.width(1)) adder_11 (
    .a(AC_INPUT[10]), .b(DR_INPUT[10]), .out(adder_11_out), .cin(adder_10_cout), .cout(adder_11_cout));
  Adder #(.width(1)) adder_12 (
    .a(AC_INPUT[11]), .b(DR_INPUT[11]), .out(adder_12_out), .cin(adder_11_cout), .cout(adder_12_cout));
  Adder #(.width(1)) adder_13 (
    .a(AC_INPUT[12]), .b(DR_INPUT[12]), .out(adder_13_out), .cin(adder_12_cout), .cout(adder_13_cout));
  Adder #(.width(1)) adder_14 (
    .a(AC_INPUT[13]), .b(DR_INPUT[13]), .out(adder_14_out), .cin(adder_13_cout), .cout(adder_14_cout));
  Adder #(.width(1)) adder_15 (
    .a(AC_INPUT[14]), .b(DR_INPUT[14]), .out(adder_15_out), .cin(adder_14_cout), .cout(adder_15_cout));
  Adder #(.width(1)) adder_16 (
    .a(AC_INPUT[15]), .b(DR_INPUT[15]), .out(adder_16_out), .cin(adder_15_cout), .cout(Cout));
  and and_1 (and_1_out, AND, AC_INPUT[0], DR_INPUT[0]);
  and and_2 (and_2_out, ADD, adder_1_out);
  and and_3 (and_3_out, DR, DR_INPUT[0]);
  and and_4 (and_4_out, INPR, INPR_INPUT[0]);
  and and_5 (and_5_out, COM, ~AC_INPUT[0]);  // AND_Gate
  and and_6 (and_6_out, SHR, AC_INPUT[1]);
  and and_7 (and_7_out, SHL, 1'b0);
  and and_8 (and_8_out, AND, AC_INPUT[1], DR_INPUT[1]);
  and u_ADD (ADD_out, ADD, adder_2_out);
  and and_9 (and_9_out, DR, DR_INPUT[1]);
  and and_10 (and_10_out, INPR, INPR_INPUT[1]);
  and and_11 (and_11_out, COM, ~AC_INPUT[1]);  // AND_Gate
  and and_12 (and_12_out, SHR, AC_INPUT[2]);
  and and_13 (and_13_out, SHL, AC_INPUT[0]);
  and AND_14 (AND_14_out, AND, AC_INPUT[2], DR_INPUT[2]);
  and and_15 (and_15_out, ADD, adder_3_out);
  and and_16 (and_16_out, DR, DR_INPUT[2]);
  and u_INPR (INPR_out, INPR, INPR_INPUT[2]);
  and u_COM (COM_out, COM, ~AC_INPUT[2]);  // AND_Gate
  and and_17 (and_17_out, SHR, AC_INPUT[3]);
  and and_18 (and_18_out, SHL, DR_INPUT[2]);
  and and_19 (and_19_out, AND, AC_INPUT[3], DR_INPUT[3]);
  and and_20 (and_20_out, ADD, adder_4_out);
  and and_21 (and_21_out, DR, DR_INPUT[3]);
  and and_22 (and_22_out, INPR, INPR_INPUT[3]);
  and and_23 (and_23_out, COM, ~AC_INPUT[3]);  // AND_Gate
  and and_24 (and_24_out, SHR, AC_INPUT[4]);
  and and_25 (and_25_out, SHL, AC_INPUT[2]);
  and and_26 (and_26_out, AND, AC_INPUT[4], DR_INPUT[4]);
  and and_27 (and_27_out, ADD, adder_5_out);
  and and_28 (and_28_out, DR, DR_INPUT[4]);
  and and_29 (and_29_out, INPR, INPR_INPUT[4]);
  and and_30 (and_30_out, COM, ~DR_INPUT[4]);  // AND_Gate
  and and_31 (and_31_out, SHR, AC_INPUT[5]);
  and and_32 (and_32_out, SHL, DR_INPUT[3]);
  and and_33 (and_33_out, AND, AC_INPUT[5], DR_INPUT[5]);
  and and_34 (and_34_out, ADD, adder_6_out);
  and and_35 (and_35_out, DR, DR_INPUT[5]);
  and and_36 (and_36_out, INPR, INPR_INPUT[5]);
  and and_37 (and_37_out, COM, ~AC_INPUT[5]);  // AND_Gate
  and and_38 (and_38_out, SHR, AC_INPUT[6]);
  and u_SHL (SHL_out, SHL, AC_INPUT[4]);
  and and_39 (and_39_out, AND, AC_INPUT[6], DR_INPUT[6]);
  and and_40 (and_40_out, ADD, adder_7_out);
  and and_41 (and_41_out, DR, DR_INPUT[6]);
  and and_42 (and_42_out, INPR, INPR_INPUT[6]);
  and and_43 (and_43_out, COM, ~AC_INPUT[6]);  // AND_Gate
  and u_SHR (SHR_out, SHR, AC_INPUT[7]);
  and and_44 (and_44_out, SHL, AC_INPUT[5]);
  and and_45 (and_45_out, AND, AC_INPUT[7], DR_INPUT[7]);
  and and_46 (and_46_out, ADD, adder_8_out);
  and and_47 (and_47_out, DR, DR_INPUT[7]);
  and and_48 (and_48_out, INPR, INPR_INPUT[7]);
  and and_49 (and_49_out, COM, ~AC_INPUT[7]);  // AND_Gate
  and and_50 (and_50_out, SHR, AC_INPUT[8]);
  and and_51 (and_51_out, SHL, AC_INPUT[6]);
  and and_52 (and_52_out, AND, AC_INPUT[8], DR_INPUT[8]);
  and and_53 (and_53_out, ADD, adder_9_out);
  and and_54 (and_54_out, DR, DR_INPUT[8]);
  and and_55 (and_55_out, COM, ~AC_INPUT[8]);  // AND_Gate
  and and_56 (and_56_out, SHR, AC_INPUT[9]);
  and and_57 (and_57_out, SHL, AC_INPUT[7]);
  and and_58 (and_58_out, AND, AC_INPUT[9], DR_INPUT[9]);
  and and_59 (and_59_out, ADD, adder_10_out);
  and and_60 (and_60_out, DR, DR_INPUT[9]);
  and and_61 (and_61_out, COM, ~AC_INPUT[9]);  // AND_Gate
  and and_62 (and_62_out, SHR, AC_INPUT[10]);
  and and_63 (and_63_out, SHL, AC_INPUT[8]);
  and and_64 (and_64_out, AND, AC_INPUT[10], DR_INPUT[10]);
  and and_65 (and_65_out, ADD, adder_11_out);
  and and_66 (and_66_out, DR, DR_INPUT[10]);
  and and_67 (and_67_out, COM, ~AC_INPUT[10]);  // AND_Gate
  and and_68 (and_68_out, SHR, AC_INPUT[11]);
  and and_69 (and_69_out, SHL, AC_INPUT[9]);
  and and_70 (and_70_out, AND, AC_INPUT[11], DR_INPUT[11]);
  and and_71 (and_71_out, ADD, adder_12_out);
  and and_72 (and_72_out, DR, DR_INPUT[11]);
  and and_73 (and_73_out, COM, ~AC_INPUT[11]);  // AND_Gate
  and and_74 (and_74_out, SHR, AC_INPUT[12]);
  and and_75 (and_75_out, SHL, AC_INPUT[10]);
  and and_76 (and_76_out, AND, AC_INPUT[12], DR_INPUT[12]);
  and and_77 (and_77_out, ADD, adder_13_out);
  and u_DR (DR_out, DR, DR_INPUT[12]);
  and and_78 (and_78_out, COM, ~AC_INPUT[12]);  // AND_Gate
  and and_79 (and_79_out, SHR, AC_INPUT[13]);
  and and_80 (and_80_out, SHL, AC_INPUT[11]);
  and and_81 (and_81_out, AND, AC_INPUT[13], DR_INPUT[13]);
  and and_82 (and_82_out, ADD, adder_14_out);
  and and_83 (and_83_out, DR, DR_INPUT[13]);
  and and_84 (and_84_out, COM, ~AC_INPUT[13]);  // AND_Gate
  and and_85 (and_85_out, SHR, AC_INPUT[14]);
  and and_86 (and_86_out, SHL, AC_INPUT[12]);
  and and_87 (and_87_out, AND, AC_INPUT[14], DR_INPUT[14]);
  and and_88 (and_88_out, ADD, adder_15_out);
  and and_89 (and_89_out, DR, DR_INPUT[14]);
  and and_90 (and_90_out, COM, ~AC_INPUT[14]);  // AND_Gate
  and and_91 (and_91_out, SHR, AC_INPUT[15]);
  and and_92 (and_92_out, SHL, AC_INPUT[13]);
  and and_93 (and_93_out, AND, AC_INPUT[15], DR_INPUT[15]);
  and and_94 (and_94_out, ADD, adder_16_out);
  and and_95 (and_95_out, DR, DR_INPUT[15]);
  and and_96 (and_96_out, COM, ~AC_INPUT[15]);  // AND_Gate
  and and_97 (and_97_out, SHR, 1'b0);
  and and_98 (and_98_out, SHL, AC_INPUT[14]);
  or I_0_7a2315b8 (I_0_7a2315b8_out, and_1_out, and_2_out, and_3_out, and_4_out, and_5_out, and_6_out, and_7_out);
  or I_1_b45e6b28 (I_1_b45e6b28_out, and_8_out, ADD_out, and_9_out, and_10_out, and_11_out, and_12_out, and_13_out);
  or I_2_e90cdf88 (I_2_e90cdf88_out, AND_14_out, and_15_out, and_16_out, INPR_out, COM_out, and_17_out, and_18_out);
  or I_3_ffe955a8 (I_3_ffe955a8_out, and_19_out, and_20_out, and_21_out, and_22_out, and_23_out, and_24_out, and_25_out);
  or I_4_3525d440 (I_4_3525d440_out, and_26_out, and_27_out, and_28_out, and_29_out, and_30_out, and_31_out, and_32_out);
  or I_5_06687591 (I_5_06687591_out, and_33_out, and_34_out, and_35_out, and_36_out, and_37_out, and_38_out, SHL_out);
  or I_6_26eeaca1 (I_6_26eeaca1_out, and_39_out, and_40_out, and_41_out, and_42_out, and_43_out, SHR_out, and_44_out);
  or I_7_1e6fe7d9 (I_7_1e6fe7d9_out, and_45_out, and_46_out, and_47_out, and_48_out, and_49_out, and_50_out, and_51_out);
  or I_8_9fd21c4f (I_8_9fd21c4f_out, and_52_out, and_53_out, and_54_out, and_55_out, and_56_out, and_57_out);
  or I_9_1a6d7d69 (I_9_1a6d7d69_out, and_58_out, and_59_out, and_60_out, and_61_out, and_62_out, and_63_out);
  or I_10_95b6212d (I_10_95b6212d_out, and_64_out, and_65_out, and_66_out, and_67_out, and_68_out, and_69_out);
  or I_11_758a845c (I_11_758a845c_out, and_70_out, and_71_out, and_72_out, and_73_out, and_74_out, and_75_out);
  or I_12_b38dc382 (I_12_b38dc382_out, and_76_out, and_77_out, DR_out, and_78_out, and_79_out, and_80_out);
  or I_13_fca28932 (I_13_fca28932_out, and_81_out, and_82_out, and_83_out, and_84_out, and_85_out, and_86_out);
  or I_14_c5212871 (I_14_c5212871_out, and_87_out, and_88_out, and_89_out, and_90_out, and_91_out, and_92_out);
  or I_15_4d47b025 (I_15_4d47b025_out, and_93_out, and_94_out, and_95_out, and_96_out, and_97_out, and_98_out);
  and and_99 (and_99_out, LD, I_0_7a2315b8_out);
  and and_100 (and_100_out, ~I_0_7a2315b8_out, LD);  // AND_Gate
  and and_101 (and_101_out, LD, I_1_b45e6b28_out);
  and and_102 (and_102_out, ~I_1_b45e6b28_out, LD);  // AND_Gate
  and and_103 (and_103_out, LD, I_2_e90cdf88_out);
  and and_104 (and_104_out, ~I_2_e90cdf88_out, LD);  // AND_Gate
  and and_105 (and_105_out, LD, I_3_ffe955a8_out);
  and and_106 (and_106_out, ~I_3_ffe955a8_out, LD);  // AND_Gate
  and and_107 (and_107_out, LD, I_4_3525d440_out);
  and and_108 (and_108_out, ~I_4_3525d440_out, LD);  // AND_Gate
  and and_109 (and_109_out, LD, I_5_06687591_out);
  and and_110 (and_110_out, ~I_5_06687591_out, LD);  // AND_Gate
  and and_111 (and_111_out, LD, I_6_26eeaca1_out);
  and and_112 (and_112_out, ~I_6_26eeaca1_out, LD);  // AND_Gate
  and and_113 (and_113_out, LD, I_7_1e6fe7d9_out);
  and and_114 (and_114_out, ~I_7_1e6fe7d9_out, LD);  // AND_Gate
  and and_115 (and_115_out, LD, I_8_9fd21c4f_out);
  and and_116 (and_116_out, ~I_8_9fd21c4f_out, LD);  // AND_Gate
  and and_117 (and_117_out, LD, I_9_1a6d7d69_out);
  and and_118 (and_118_out, ~I_9_1a6d7d69_out, LD);  // AND_Gate
  and and_119 (and_119_out, LD, I_10_95b6212d_out);
  and and_120 (and_120_out, ~I_10_95b6212d_out, LD);  // AND_Gate
  and and_121 (and_121_out, LD, I_11_758a845c_out);
  and and_122 (and_122_out, ~I_11_758a845c_out, LD);  // AND_Gate
  and and_123 (and_123_out, LD, I_12_b38dc382_out);
  and and_124 (and_124_out, ~I_12_b38dc382_out, LD);  // AND_Gate
  and and_125 (and_125_out, LD, I_13_fca28932_out);
  and and_126 (and_126_out, ~I_13_fca28932_out, LD);  // AND_Gate
  and and_127 (and_127_out, LD, I_14_c5212871_out);
  and and_128 (and_128_out, ~I_14_c5212871_out, LD);  // AND_Gate
  and and_129 (and_129_out, LD, I_15_4d47b025_out);
  and and_130 (and_130_out, ~I_15_4d47b025_out, LD);  // AND_Gate
  J_K_Flip_Flop j_k_ff_1 (.J(and_99_out), .clk(CLK), .K(and_100_out), .Q(OUTPUT[0]));  // open: Qn, preset, en, reset
  J_K_Flip_Flop j_k_ff_2 (.J(and_101_out), .clk(CLK), .K(and_102_out), .Q(OUTPUT[1]));  // open: Qn, preset, en, reset
  J_K_Flip_Flop j_k_ff_3 (.J(and_103_out), .clk(CLK), .K(and_104_out), .Q(OUTPUT[2]));  // open: Qn, preset, en, reset
  J_K_Flip_Flop j_k_ff_4 (.J(and_105_out), .clk(CLK), .K(and_106_out), .Q(OUTPUT[3]));  // open: Qn, preset, en, reset
  J_K_Flip_Flop j_k_ff_5 (.J(and_107_out), .clk(CLK), .K(and_108_out), .Q(OUTPUT[4]));  // open: Qn, preset, en, reset
  J_K_Flip_Flop j_k_ff_6 (.J(and_109_out), .clk(CLK), .K(and_110_out), .Q(OUTPUT[5]));  // open: Qn, preset, en, reset
  J_K_Flip_Flop j_k_ff_7 (.J(and_111_out), .clk(CLK), .K(and_112_out), .Q(OUTPUT[6]));  // open: Qn, preset, en, reset
  J_K_Flip_Flop j_k_ff_8 (.J(and_113_out), .clk(CLK), .K(and_114_out), .Q(OUTPUT[7]));  // open: Qn, preset, en, reset
  J_K_Flip_Flop j_k_ff_9 (.J(and_115_out), .clk(CLK), .K(and_116_out), .Q(OUTPUT[8]));  // open: Qn, preset, en, reset
  J_K_Flip_Flop j_k_ff_10 (.J(and_117_out), .clk(CLK), .K(and_118_out), .Q(OUTPUT[9]));  // open: Qn, preset, en, reset
  J_K_Flip_Flop j_k_ff_11 (.J(and_119_out), .clk(CLK), .K(and_120_out), .Q(OUTPUT[10]));  // open: Qn, preset, en, reset
  J_K_Flip_Flop j_k_ff_12 (.J(and_121_out), .clk(CLK), .K(and_122_out), .Q(OUTPUT[11]));  // open: Qn, preset, en, reset
  J_K_Flip_Flop j_k_ff_13 (.J(and_123_out), .clk(CLK), .K(and_124_out), .Q(OUTPUT[12]));  // open: Qn, preset, en, reset
  J_K_Flip_Flop j_k_ff_14 (.J(and_125_out), .clk(CLK), .K(and_126_out), .Q(OUTPUT[13]));  // open: Qn, preset, en, reset
  J_K_Flip_Flop j_k_ff_15 (.J(and_127_out), .clk(CLK), .K(and_128_out), .Q(OUTPUT[14]));  // open: Qn, preset, en, reset
  J_K_Flip_Flop j_k_ff_16 (.J(and_129_out), .clk(CLK), .K(and_130_out), .Q(OUTPUT[15]));  // open: Qn, preset, en, reset
endmodule

module L_8_Bit_Bus (
  input  [2:0] SELECT,
  input  [11:0] AR_1,
  input  [11:0] DR_2,
  input  [15:0] AC_3,
  input  [15:0] IR_4,
  input  [15:0] TR_5,
  input  [15:0] TR_6,
  input  [15:0] IR_7,
  output Output_0,
  output Output_1,
  output Output_2,
  output Output_3,
  output Output_4,
  output Output_5,
  output Output_6,
  output Output_7
);

  Multiplexer #(.select(3), .enable("false")) multiplexer_1 (
    .in0(1'b0), .in1(AR_1[0]), .in2(DR_2[0]), .in3(AC_3[0]), .in4(IR_4[0]), .in5(TR_5[0]), .in6(TR_6[0]),
    .in7(IR_7[0]), .out(Output_0), .sel(SELECT));
  Multiplexer #(.select(3), .enable("false")) multiplexer_2 (
    .in0(1'b0), .in1(AR_1[1]), .in2(DR_2[1]), .in3(AC_3[1]), .in4(IR_4[1]), .in5(TR_5[1]), .in6(TR_6[1]),
    .in7(IR_7[1]), .out(Output_1), .sel(SELECT));
  Multiplexer #(.select(3), .enable("false")) multiplexer_3 (
    .in0(1'b0), .in1(AR_1[2]), .in2(DR_2[2]), .in3(AC_3[2]), .in4(IR_4[2]), .in5(TR_5[2]), .in6(TR_6[2]),
    .in7(IR_7[2]), .out(Output_2), .sel(SELECT));
  Multiplexer #(.select(3), .enable("false")) multiplexer_4 (
    .in0(1'b0), .in1(AR_1[3]), .in2(DR_2[3]), .in3(AC_3[3]), .in4(IR_4[3]), .in5(TR_5[3]), .in6(TR_6[3]),
    .in7(IR_7[3]), .out(Output_3), .sel(SELECT));
  Multiplexer #(.select(3), .enable("false")) multiplexer_5 (
    .in0(1'b0), .in1(AR_1[4]), .in2(DR_2[4]), .in3(AC_3[4]), .in4(IR_4[4]), .in5(TR_5[4]), .in6(TR_6[4]),
    .in7(IR_7[4]), .out(Output_4), .sel(SELECT));
  Multiplexer #(.select(3), .enable("false")) multiplexer_6 (
    .in0(1'b0), .in1(AR_1[5]), .in2(DR_2[5]), .in3(AC_3[5]), .in4(IR_4[5]), .in5(TR_5[5]), .in6(TR_6[5]),
    .in7(IR_7[5]), .out(Output_5), .sel(SELECT));
  Multiplexer #(.select(3), .enable("false")) multiplexer_7 (
    .in0(1'b0), .in1(AR_1[6]), .in2(DR_2[6]), .in3(AC_3[6]), .in4(IR_4[6]), .in5(TR_5[6]), .in6(TR_6[6]),
    .in7(IR_7[6]), .out(Output_6), .sel(SELECT));
  Multiplexer #(.select(3), .enable("false")) multiplexer_8 (
    .in0(1'b0), .in1(AR_1[7]), .in2(DR_2[7]), .in3(AC_3[7]), .in4(IR_4[7]), .in5(TR_5[7]), .in6(TR_6[7]),
    .in7(IR_7[7]), .out(Output_7), .sel(SELECT));
endmodule
